// Digital circuit day2.dig as structural Verilog
module day2 (
  input  clock
);

  wire and_1_out, and_2_out, comparator_1_eq, comparator_2_eq, comparator_3_eq, comparator_4_eq,
       comparator_5_eq, comparator_6_eq, decoder_1_out_1, decoder_1_out_2, decoder_1_out_3, run_q;
  wire [1:0] ilen_out, phase_out;
  wire [15:0] add_1_s, add_2_s, pc_q, ram_d2;
  wire [31:0] cycles_out, icount_out, Y_q;
  wire [63:0] at_0_q, instr_q, mul_mul, multiplexer_1_out, plus_s, ram_d1, X_q;
  wire [63:16] ram_d2_2;
  wire [63:32] Y_q_2;

  // Probe on at_0_q
  LED running (.in(run_q));
  and and_1 (and_1_out, run_q, clock);
  Register #(.Bits(64)) at_0 (.D(multiplexer_1_out), .C(and_1_out), .en(and_2_out), .Q(at_0_q));
  Counter #(.Bits(32)) cycles (.en(run_q), .C(and_1_out), .clr(1'b0), .out(cycles_out));  // open: ovf
  and and_2 (and_2_out, comparator_1_eq, decoder_1_out_3);
  T_FF #(.Default(1)) run (.T(comparator_4_eq), .C(and_1_out), .Q(run_q));  // open: nQ
  // Probe on cycles_out
  Comparator #(.Bits(16)) comparator_1 (.a({16{1'b0}}), .b(ram_d2), .eq(comparator_1_eq));  // open: gt, lt
  Add #(.Bits(16)) add_1 (.a({{14{1'b0}}, phase_out}), .b(pc_q), .c_i(1'b0), .s(add_1_s));  // open: c_o
  RAMDualAccess #(.AddrBits(16), .Bits(64), .isProgramMemory("true")) ram (
    .str(decoder_1_out_3), .C(and_1_out), .ld(1'b1), .A1(ram_d2), .Din1(multiplexer_1_out), .A2(add_1_s),
    .D1(ram_d1), .D2({ram_d2_2, ram_d2}));
  Add #(.Bits(16)) add_2 (.a(pc_q), .b({{14{1'b0}}, ilen_out}), .c_i(1'b1), .s(add_2_s));  // open: c_o
  Register #(.Bits(16), .isProgramCounter("true")) pc (.D(add_2_s), .C(and_1_out), .en(comparator_2_eq), .Q(pc_q));
  // Probe on pc_q
  Counter #(.Bits(32)) icount (.en(comparator_3_eq), .C(and_1_out), .clr(1'b0), .out(icount_out));  // open: ovf
  Counter #(.Bits(2)) phase (.en(1'b1), .C(and_1_out), .clr(comparator_2_eq), .out(phase_out));  // open: ovf
  Comparator #(.Bits(2)) comparator_2 (.a(phase_out), .b(ilen_out), .eq(comparator_2_eq));  // open: gt, lt
  // Probe on icount_out
  Register #(.Bits(64)) instr (.D({ram_d2_2, ram_d2}), .C(and_1_out), .en(comparator_3_eq), .Q(instr_q));
  Comparator #(.Bits(2)) comparator_3 (.a(phase_out), .b(2'b00), .eq(comparator_3_eq));  // open: gt, lt
  // Probe on phase_out
  // Probe on instr_q
  Comparator #(.Bits(64), .Signed("true")) comparator_4 (
    .a(instr_q), .b(64'h63), .eq(comparator_4_eq));  // open: gt, lt
  Decoder #(.Selector_Bits(2)) decoder_1 (
    .sel(phase_out), .out_1(decoder_1_out_1), .out_2(decoder_1_out_2), .out_3(decoder_1_out_3));  // open: out_0
  LookUpTable #(.Bits(2)) ilen (.in0(comparator_4_eq), .in1(comparator_5_eq), .in2(comparator_6_eq), .out(ilen_out));
  // Probe on ilen_out
  Comparator #(.Signed("true"), .Bits(64)) comparator_5 (.a(instr_q), .b(64'h1), .eq(comparator_5_eq));  // open: gt, lt
  Register #(.Bits(64)) X (.D(ram_d1), .C(and_1_out), .en(decoder_1_out_1), .Q(X_q));
  Add #(.Bits(64)) plus (.a(X_q), .b({Y_q_2, Y_q}), .c_i(1'b0), .s(plus_s));  // open: c_o
  // Probe on X_q
  Comparator #(.Signed("true"), .Bits(64)) comparator_6 (.a(instr_q), .b(64'h2), .eq(comparator_6_eq));  // open: gt, lt
  Register #(.Bits(64)) Y (.D(ram_d1), .C(and_1_out), .en(decoder_1_out_2), .Q({Y_q_2, Y_q}));
  Mul #(.Bits(32), .Signed("true")) mul (.a(Y_q), .b(X_q[31:0]), .mul(mul_mul));
  // Probe on {Y_q_2, Y_q}
  Multiplexer #(.Bits(64)) multiplexer_1 (
    .sel(comparator_6_eq), .in_0(plus_s), .in_1(mul_mul), .out(multiplexer_1_out));
  // Probe r on multiplexer_1_out

  // Notes on the sheet:
  //   clock: Hz: 1000
  //   Instruction decoding
  //   Internal registers
  //   contents of ilen (hex, n*v repeats v):
  //   1,1,3,1,3,1,1,1
  //   ALU
endmodule
