// Digital circuit day23.dig as structural Verilog
module day23 (
  input  C,
  output [31:0] cycles,
  output [63:0] Y
);

  wire and_1_out, and_3_out, C_t, comparator_1_gt, comparator_2_lt, comparator_3_eq, comparator_4_eq,
       comparator_5_eq, day23_parser_1_nextout_en, day23_parser_1_out_en, day23_parser_1_out_y,
       demultiplexer_1_out_0, demultiplexer_1_out_1, node0_p3, node0_p5, node0_p7, node0_p9, node0_p10,
       node0_p11, node0_p13, node0_p15, node0_p17, node0_p21, node0_p22, node0_p23, node1_out_en,
       node2_out_en, node3_out_en, node4_out_en, node5_out_en, node6_out_en, node7_out_en, node8_out_en,
       node9_out_en, node10_out_en, node11_out_en, node12_out_en, node13_out_en, node14_out_en,
       node15_out_en, node16_out_en, node17_out_en, node18_out_en, node19_out_en, node20_out_en,
       node21_out_en, node22_out_en, node23_out_en, node24_out_en, node25_out_en, node26_out_en,
       node27_out_en, node28_out_en, node29_out_en, node30_out_en, node31_out_en, node32_out_en,
       node33_out_en, node34_out_en, node35_out_en, node36_out_en, node37_out_en, node38_out_en,
       node39_out_en, node40_out_en, node41_out_en, node42_out_en, node43_out_en, node44_out_en,
       node45_out_en, node46_out_en, node47_out_en, node48_out_en, node49_p1, node49_p3, node49_p6,
       node49_p7, node49_p10, node49_p11, node49_p12, node49_p16, node49_p17, not_1_out, or_1_out,
       shifter_1_p5, shifter_1_p8, shifter_1_p9, shifter_1_p10, shifter_1_p11;
  wire [3:0] div_1_r, div_2_r, div_3_r, div_4_r, div_5_r, phase_out;
  wire [31:0] node1_out_cnt, node2_out_cnt, node3_out_cnt, node4_out_cnt, node5_out_cnt, node6_out_cnt,
       node7_out_cnt, node8_out_cnt, node9_out_cnt, node10_out_cnt, node11_out_cnt, node12_out_cnt,
       node13_out_cnt, node14_out_cnt, node15_out_cnt, node16_out_cnt, node17_out_cnt, node18_out_cnt,
       node19_out_cnt, node20_out_cnt, node21_out_cnt, node22_out_cnt, node23_out_cnt, node24_out_cnt,
       node25_out_cnt, node26_out_cnt, node27_out_cnt, node28_out_cnt, node29_out_cnt, node30_out_cnt,
       node31_out_cnt, node32_out_cnt, node33_out_cnt, node34_out_cnt, node35_out_cnt, node36_out_cnt,
       node37_out_cnt, node38_out_cnt, node39_out_cnt, node40_out_cnt, node41_out_cnt, node42_out_cnt,
       node43_out_cnt, node44_out_cnt, node45_out_cnt, node46_out_cnt, node47_out_cnt, node48_out_cnt;
  wire [63:0] day23_parser_1_nextout_val, day23_parser_1_out_val, div_2_q, div_3_q, div_4_q, div_5_q,
       node0_p12, node0_p20, node1_out_val, node2_out_val, node3_out_val, node4_out_val, node5_out_val,
       node6_out_val, node7_out_val, node8_out_val, node9_out_val, node10_out_val, node11_out_val,
       node12_out_val, node13_out_val, node14_out_val, node15_out_val, node16_out_val, node17_out_val,
       node18_out_val, node19_out_val, node20_out_val, node21_out_val, node22_out_val, node23_out_val,
       node24_out_val, node25_out_val, node26_out_val, node27_out_val, node28_out_val, node29_out_val,
       node30_out_val, node31_out_val, node32_out_val, node33_out_val, node34_out_val, node35_out_val,
       node36_out_val, node37_out_val, node38_out_val, node39_out_val, node40_out_val, node41_out_val,
       node42_out_val, node43_out_val, node44_out_val, node45_out_val, node46_out_val, node47_out_val,
       node48_out_val, node49_p14, shifter_1_p2, shifter_1_p6, shifter_1_p7, X_q, Y_q;
  wire [63:4] div_1_r_2, div_2_r_2, div_3_r_2, div_4_r_2, div_5_r_2;

  // day23_node #(.generic("label := \"node0\";")) node0: pin names not known; wires that end beside it: C_t, {64{1'b0}}, node0_p3, node0_p3, node0_p5, node0_p5, node0_p7, node0_p7, node0_p9, node0_p10, node0_p11, node0_p12, node0_p13, node0_p13, node0_p15, node0_p15, node0_p17, node0_p17, 1'b0, node0_p20, node0_p21, node0_p22, node0_p23
  day23_node #(.generic("label := \"node1\";")) node1 (
    .C(C_t), .out_en(node1_out_en), .out_val(node1_out_val), .in_en(node0_p11), .in_val(node0_p20),
    .out_cnt(node1_out_cnt));  // open: addr_next, out_busy, addr, in_busy
  day23_node #(.generic("label := \"node2\";")) node2 (
    .C(C_t), .out_en(node2_out_en), .out_val(node2_out_val), .in_en(node1_out_en), .in_val(node1_out_val),
    .out_cnt(node2_out_cnt));  // open: addr_next, out_busy, addr, in_busy
  day23_node #(.generic("label := \"node3\";")) node3 (
    .C(C_t), .out_en(node3_out_en), .out_val(node3_out_val), .in_en(node2_out_en), .in_val(node2_out_val),
    .out_cnt(node3_out_cnt));  // open: addr_next, out_busy, addr, in_busy
  day23_node #(.generic("label := \"node4\";")) node4 (
    .C(C_t), .out_en(node4_out_en), .out_val(node4_out_val), .in_en(node3_out_en), .in_val(node3_out_val),
    .out_cnt(node4_out_cnt));  // open: addr_next, out_busy, addr, in_busy
  day23_node #(.generic("label := \"node5\";")) node5 (
    .C(C_t), .out_en(node5_out_en), .out_val(node5_out_val), .in_en(node4_out_en), .in_val(node4_out_val),
    .out_cnt(node5_out_cnt));  // open: addr_next, out_busy, addr, in_busy
  day23_node #(.generic("label := \"node6\";")) node6 (
    .C(C_t), .out_en(node6_out_en), .out_val(node6_out_val), .in_en(node5_out_en), .in_val(node5_out_val),
    .out_cnt(node6_out_cnt));  // open: addr_next, out_busy, addr, in_busy
  day23_node #(.generic("label := \"node7\";")) node7 (
    .C(C_t), .out_en(node7_out_en), .out_val(node7_out_val), .in_en(node6_out_en), .in_val(node6_out_val),
    .out_cnt(node7_out_cnt));  // open: addr_next, out_busy, addr, in_busy
  day23_node #(.generic("label := \"node8\";")) node8 (
    .C(C_t), .out_en(node8_out_en), .out_val(node8_out_val), .in_en(node7_out_en), .in_val(node7_out_val),
    .out_cnt(node8_out_cnt));  // open: addr_next, out_busy, addr, in_busy
  day23_node #(.generic("label := \"node9\";")) node9 (
    .C(C_t), .out_en(node9_out_en), .out_val(node9_out_val), .in_en(node8_out_en), .in_val(node8_out_val),
    .out_cnt(node9_out_cnt));  // open: addr_next, out_busy, addr, in_busy
  day23_node #(.generic("label := \"node10\";")) node10 (
    .C(C_t), .out_en(node10_out_en), .out_val(node10_out_val), .in_en(node9_out_en), .in_val(node9_out_val),
    .out_cnt(node10_out_cnt));  // open: addr_next, out_busy, addr, in_busy
  day23_node #(.generic("label := \"node11\";")) node11 (
    .C(C_t), .out_en(node11_out_en), .out_val(node11_out_val), .in_en(node10_out_en),
    .in_val(node10_out_val), .out_cnt(node11_out_cnt));  // open: addr_next, out_busy, addr, in_busy
  day23_node #(.generic("label := \"node12\";")) node12 (
    .C(C_t), .out_en(node12_out_en), .out_val(node12_out_val), .in_en(node11_out_en),
    .in_val(node11_out_val), .out_cnt(node12_out_cnt));  // open: addr_next, out_busy, addr, in_busy
  day23_node #(.generic("label := \"node13\";")) node13 (
    .C(C_t), .out_en(node13_out_en), .out_val(node13_out_val), .in_en(node12_out_en),
    .in_val(node12_out_val), .out_cnt(node13_out_cnt));  // open: addr_next, out_busy, addr, in_busy
  day23_node #(.generic("label := \"node14\";")) node14 (
    .C(C_t), .out_en(node14_out_en), .out_val(node14_out_val), .in_en(node13_out_en),
    .in_val(node13_out_val), .out_cnt(node14_out_cnt));  // open: addr_next, out_busy, addr, in_busy
  day23_node #(.generic("label := \"node15\";")) node15 (
    .C(C_t), .out_en(node15_out_en), .out_val(node15_out_val), .in_en(node14_out_en),
    .in_val(node14_out_val), .out_cnt(node15_out_cnt));  // open: addr_next, out_busy, addr, in_busy
  // Probe on node0_p21
  // Probe on node1_out_cnt
  // Probe on node2_out_cnt
  // Probe on node3_out_cnt
  // Probe on node4_out_cnt
  // Probe on node5_out_cnt
  // Probe on node6_out_cnt
  // Probe on node7_out_cnt
  // Probe on node8_out_cnt
  // Probe on node9_out_cnt
  // Probe on node10_out_cnt
  // Probe on node11_out_cnt
  // Probe on node12_out_cnt
  // Probe on node13_out_cnt
  // Probe on node14_out_cnt
  // Probe on node15_out_cnt
  day23_node #(.generic("label := \"node16\";")) node16 (
    .C(C_t), .out_en(node16_out_en), .out_val(node16_out_val), .in_en(node15_out_en),
    .in_val(node15_out_val), .out_cnt(node16_out_cnt));  // open: addr_next, out_busy, addr, in_busy
  day23_node #(.generic("label := \"node17\";")) node17 (
    .C(C_t), .out_en(node17_out_en), .out_val(node17_out_val), .in_en(node16_out_en),
    .in_val(node16_out_val), .out_cnt(node17_out_cnt));  // open: addr_next, out_busy, addr, in_busy
  day23_node #(.generic("label := \"node18\";")) node18 (
    .C(C_t), .out_en(node18_out_en), .out_val(node18_out_val), .in_en(node17_out_en),
    .in_val(node17_out_val), .out_cnt(node18_out_cnt));  // open: addr_next, out_busy, addr, in_busy
  day23_node #(.generic("label := \"node19\";")) node19 (
    .C(C_t), .out_en(node19_out_en), .out_val(node19_out_val), .in_en(node18_out_en),
    .in_val(node18_out_val), .out_cnt(node19_out_cnt));  // open: addr_next, out_busy, addr, in_busy
  day23_node #(.generic("label := \"node20\";")) node20 (
    .C(C_t), .out_en(node20_out_en), .out_val(node20_out_val), .in_en(node19_out_en),
    .in_val(node19_out_val), .out_cnt(node20_out_cnt));  // open: addr_next, out_busy, addr, in_busy
  day23_node #(.generic("label := \"node21\";")) node21 (
    .C(C_t), .out_en(node21_out_en), .out_val(node21_out_val), .in_en(node20_out_en),
    .in_val(node20_out_val), .out_cnt(node21_out_cnt));  // open: addr_next, out_busy, addr, in_busy
  day23_node #(.generic("label := \"node22\";")) node22 (
    .C(C_t), .out_en(node22_out_en), .out_val(node22_out_val), .in_en(node21_out_en),
    .in_val(node21_out_val), .out_cnt(node22_out_cnt));  // open: addr_next, out_busy, addr, in_busy
  day23_node #(.generic("label := \"node23\";")) node23 (
    .C(C_t), .out_en(node23_out_en), .out_val(node23_out_val), .in_en(node22_out_en),
    .in_val(node22_out_val), .out_cnt(node23_out_cnt));  // open: addr_next, out_busy, addr, in_busy
  day23_node #(.generic("label := \"node24\";")) node24 (
    .C(C_t), .out_en(node24_out_en), .out_val(node24_out_val), .in_en(node23_out_en),
    .in_val(node23_out_val), .out_cnt(node24_out_cnt));  // open: addr_next, out_busy, addr, in_busy
  day23_node #(.generic("label := \"node25\";")) node25 (
    .C(C_t), .out_en(node25_out_en), .out_val(node25_out_val), .in_en(node24_out_en),
    .in_val(node24_out_val), .out_cnt(node25_out_cnt));  // open: addr_next, out_busy, addr, in_busy
  day23_node #(.generic("label := \"node26\";")) node26 (
    .C(C_t), .out_en(node26_out_en), .out_val(node26_out_val), .in_en(node25_out_en),
    .in_val(node25_out_val), .out_cnt(node26_out_cnt));  // open: addr_next, out_busy, addr, in_busy
  day23_node #(.generic("label := \"node27\";")) node27 (
    .C(C_t), .out_en(node27_out_en), .out_val(node27_out_val), .in_en(node26_out_en),
    .in_val(node26_out_val), .out_cnt(node27_out_cnt));  // open: addr_next, out_busy, addr, in_busy
  day23_node #(.generic("label := \"node28\";")) node28 (
    .C(C_t), .out_en(node28_out_en), .out_val(node28_out_val), .in_en(node27_out_en),
    .in_val(node27_out_val), .out_cnt(node28_out_cnt));  // open: addr_next, out_busy, addr, in_busy
  day23_node #(.generic("label := \"node29\";")) node29 (
    .C(C_t), .out_en(node29_out_en), .out_val(node29_out_val), .in_en(node28_out_en),
    .in_val(node28_out_val), .out_cnt(node29_out_cnt));  // open: addr_next, out_busy, addr, in_busy
  day23_node #(.generic("label := \"node30\";")) node30 (
    .C(C_t), .out_en(node30_out_en), .out_val(node30_out_val), .in_en(node29_out_en),
    .in_val(node29_out_val), .out_cnt(node30_out_cnt));  // open: addr_next, out_busy, addr, in_busy
  day23_node #(.generic("label := \"node31\";")) node31 (
    .C(C_t), .out_en(node31_out_en), .out_val(node31_out_val), .in_en(node30_out_en),
    .in_val(node30_out_val), .out_cnt(node31_out_cnt));  // open: addr_next, out_busy, addr, in_busy
  // Probe on node16_out_cnt
  // Probe on node17_out_cnt
  // Probe on node18_out_cnt
  // Probe on node19_out_cnt
  // Probe on node20_out_cnt
  // Probe on node21_out_cnt
  // Probe on node22_out_cnt
  // Probe on node23_out_cnt
  // Probe on node24_out_cnt
  // Probe on node25_out_cnt
  // Probe on node26_out_cnt
  // Probe on node27_out_cnt
  // Probe on node28_out_cnt
  // Probe on node29_out_cnt
  // Probe on node30_out_cnt
  // Probe on node31_out_cnt
  day23_node #(.generic("label := \"node32\";")) node32 (
    .C(C_t), .out_en(node32_out_en), .out_val(node32_out_val), .in_en(node31_out_en),
    .in_val(node31_out_val), .out_cnt(node32_out_cnt));  // open: addr_next, out_busy, addr, in_busy
  day23_node #(.generic("label := \"node33\";")) node33 (
    .C(C_t), .out_en(node33_out_en), .out_val(node33_out_val), .in_en(node32_out_en),
    .in_val(node32_out_val), .out_cnt(node33_out_cnt));  // open: addr_next, out_busy, addr, in_busy
  day23_node #(.generic("label := \"node34\";")) node34 (
    .C(C_t), .out_en(node34_out_en), .out_val(node34_out_val), .in_en(node33_out_en),
    .in_val(node33_out_val), .out_cnt(node34_out_cnt));  // open: addr_next, out_busy, addr, in_busy
  day23_node #(.generic("label := \"node35\";")) node35 (
    .C(C_t), .out_en(node35_out_en), .out_val(node35_out_val), .in_en(node34_out_en),
    .in_val(node34_out_val), .out_cnt(node35_out_cnt));  // open: addr_next, out_busy, addr, in_busy
  day23_node #(.generic("label := \"node36\";")) node36 (
    .C(C_t), .out_en(node36_out_en), .out_val(node36_out_val), .in_en(node35_out_en),
    .in_val(node35_out_val), .out_cnt(node36_out_cnt));  // open: addr_next, out_busy, addr, in_busy
  day23_node #(.generic("label := \"node37\";")) node37 (
    .C(C_t), .out_en(node37_out_en), .out_val(node37_out_val), .in_en(node36_out_en),
    .in_val(node36_out_val), .out_cnt(node37_out_cnt));  // open: addr_next, out_busy, addr, in_busy
  day23_node #(.generic("label := \"node38\";")) node38 (
    .C(C_t), .out_en(node38_out_en), .out_val(node38_out_val), .in_en(node37_out_en),
    .in_val(node37_out_val), .out_cnt(node38_out_cnt));  // open: addr_next, out_busy, addr, in_busy
  day23_node #(.generic("label := \"node39\";")) node39 (
    .C(C_t), .out_en(node39_out_en), .out_val(node39_out_val), .in_en(node38_out_en),
    .in_val(node38_out_val), .out_cnt(node39_out_cnt));  // open: addr_next, out_busy, addr, in_busy
  day23_node #(.generic("label := \"node40\";")) node40 (
    .C(C_t), .out_en(node40_out_en), .out_val(node40_out_val), .in_en(node39_out_en),
    .in_val(node39_out_val), .out_cnt(node40_out_cnt));  // open: addr_next, out_busy, addr, in_busy
  day23_node #(.generic("label := \"node41\";")) node41 (
    .C(C_t), .out_en(node41_out_en), .out_val(node41_out_val), .in_en(node40_out_en),
    .in_val(node40_out_val), .out_cnt(node41_out_cnt));  // open: addr_next, out_busy, addr, in_busy
  day23_node #(.generic("label := \"node42\";")) node42 (
    .C(C_t), .out_en(node42_out_en), .out_val(node42_out_val), .in_en(node41_out_en),
    .in_val(node41_out_val), .out_cnt(node42_out_cnt));  // open: addr_next, out_busy, addr, in_busy
  day23_node #(.generic("label := \"node43\";")) node43 (
    .C(C_t), .out_en(node43_out_en), .out_val(node43_out_val), .in_en(node42_out_en),
    .in_val(node42_out_val), .out_cnt(node43_out_cnt));  // open: addr_next, out_busy, addr, in_busy
  day23_node #(.generic("label := \"node44\";")) node44 (
    .C(C_t), .out_en(node44_out_en), .out_val(node44_out_val), .in_en(node43_out_en),
    .in_val(node43_out_val), .out_cnt(node44_out_cnt));  // open: addr_next, out_busy, addr, in_busy
  day23_node #(.generic("label := \"node45\";")) node45 (
    .C(C_t), .out_en(node45_out_en), .out_val(node45_out_val), .in_en(node44_out_en),
    .in_val(node44_out_val), .out_cnt(node45_out_cnt));  // open: addr_next, out_busy, addr, in_busy
  day23_node #(.generic("label := \"node46\";")) node46 (
    .C(C_t), .out_en(node46_out_en), .out_val(node46_out_val), .in_en(node45_out_en),
    .in_val(node45_out_val), .out_cnt(node46_out_cnt));  // open: addr_next, out_busy, addr, in_busy
  day23_node #(.generic("label := \"node47\";")) node47 (
    .C(C_t), .out_en(node47_out_en), .out_val(node47_out_val), .in_en(node46_out_en),
    .in_val(node46_out_val), .out_cnt(node47_out_cnt));  // open: addr_next, out_busy, addr, in_busy
  // Probe on node32_out_cnt
  // Probe on node33_out_cnt
  // Probe on node34_out_cnt
  // Probe on node35_out_cnt
  // Probe on node36_out_cnt
  // Probe on node37_out_cnt
  // Probe on node38_out_cnt
  // Probe on node39_out_cnt
  // Probe on node40_out_cnt
  // Probe on node41_out_cnt
  // Probe on node42_out_cnt
  // Probe on node43_out_cnt
  // Probe on node44_out_cnt
  // Probe on node45_out_cnt
  // Probe on node46_out_cnt
  // Probe on node47_out_cnt
  day23_node #(.generic("label := \"node48\";")) node48 (
    .C(C_t), .out_en(node48_out_en), .out_val(node48_out_val), .in_en(node47_out_en),
    .in_val(node47_out_val), .out_cnt(node48_out_cnt));  // open: addr_next, out_busy, addr, in_busy
  // day23_node #(.generic("label := \"node49\";")) node49: pin names not known; wires that end beside it: node49_p1, node49_p1, node49_p3, node49_p3, C_t, node49_p6, node49_p7, node49_p7, node48_out_en, node49_p10, node49_p11, node49_p12, node49_p12, node49_p14, node48_out_val, node49_p16, node49_p17
  Seven_Seg_Hex seven_seg_hex_1 (.d(div_1_r), .dp(1'b0));
  Div #(.Bits(64)) div_1 (.a(div_2_q), .b(64'ha), .r({div_1_r_2, div_1_r}));  // open: q
  Seven_Seg_Hex seven_seg_hex_2 (.d(div_2_r), .dp(1'b0));
  Div #(.Bits(64)) div_2 (.a(div_3_q), .b(64'ha), .q(div_2_q), .r({div_2_r_2, div_2_r}));
  not not_1 (not_1_out, node49_p16);
  day23_parser day23_parser_1 (
    .in_en(node49_p10), .in_val(node49_p14), .address(64'hff), .C(C_t), .out_en(day23_parser_1_out_en),
    .out_val(day23_parser_1_out_val), .nextout_en(day23_parser_1_nextout_en),
    .nextout_val(day23_parser_1_nextout_val), .out_y(day23_parser_1_out_y));
  Seven_Seg_Hex seven_seg_hex_3 (.d(div_3_r), .dp(1'b0));
  // Probe on node48_out_cnt
  // Probe on node49_p17
  Div #(.Bits(64)) div_3 (.a(div_4_q), .b(64'ha), .q(div_3_q), .r({div_3_r_2, div_3_r}));
  Seven_Seg_Hex seven_seg_hex_4 (.d(div_4_r), .dp(1'b0));
  Div #(.Bits(64)) div_4 (.a(div_5_q), .b(64'ha), .q(div_4_q), .r({div_4_r_2, div_4_r}));
  Seven_Seg_Hex seven_seg_hex_5 (.d(div_5_r), .dp(and_3_out));
  Div #(.Bits(64)) div_5 (.a(Y), .b(64'ha), .q(div_5_q), .r({div_5_r_2, div_5_r}));
  Comparator #(.Bits(4)) comparator_1 (.a(phase_out), .b(4'b0000), .gt(comparator_1_gt));  // open: eq, lt
  Comparator #(.Bits(4)) comparator_2 (.a(phase_out), .b(4'b0011), .lt(comparator_2_lt));  // open: gt, eq
  Demultiplexer demultiplexer_1 (
    .sel(day23_parser_1_out_y), .in(day23_parser_1_out_en), .out_0(demultiplexer_1_out_0),
    .out_1(demultiplexer_1_out_1));
  or or_1 (or_1_out, not_1_out, comparator_1_gt);
  Register #(.Bits(64)) X (.D(day23_parser_1_out_val), .C(C_t), .en(demultiplexer_1_out_0), .Q(X_q));
  and and_1 (and_1_out, or_1_out, comparator_2_lt);
  // shifter shifter_1: pin names not known; wires that end beside it: and_1_out, shifter_1_p2, C_t, Y, shifter_1_p5, shifter_1_p6, shifter_1_p7, shifter_1_p8, shifter_1_p9, shifter_1_p10, shifter_1_p11
  // Probe on X_q
  Counter #(.Bits(4)) phase (.en(or_1_out), .C(C_t), .clr(1'b0), .out(phase_out));  // open: ovf
  Counter #(.Bits(32)) u_cycles (.en(1'b1), .C(C_t), .clr(1'b0), .out(cycles));  // open: ovf
  Register #(.Bits(64)) u_Y (.D(day23_parser_1_out_val), .C(C_t), .en(demultiplexer_1_out_1), .Q(Y_q));
  Multiplexer #(.Selector_Bits(2), .Bits(64)) multiplexer_1 (
    .sel(phase_out[1:0]), .in_0({64{1'b0}}), .in_1(X_q), .in_2(Y_q), .in_3({64{1'b0}}), .out(shifter_1_p2));
  day23_merger day23_merger_1 (
    .C(C_t), .in1_en(and_1_out), .in1_val(shifter_1_p2), .in2_en(day23_parser_1_nextout_en),
    .in2_val(day23_parser_1_nextout_val), .out_en(node0_p10), .out_val(node0_p12));  // open: out_busy
  Comparator #(.Bits(64)) comparator_3 (.a(shifter_1_p6), .b({64{1'b0}}), .eq(comparator_3_eq));  // open: gt, lt
  // Probe on cycles
  // Probe on Y_q
  Comparator #(.Bits(64)) comparator_4 (.a(shifter_1_p7), .b(Y), .eq(comparator_4_eq));  // open: gt, lt
  and and_2 (C_t, ~and_3_out, C);  // And
  and and_3 (and_3_out, ~comparator_5_eq, comparator_4_eq, comparator_3_eq);  // And
  Break #(.Cycles(420000)) stable (.brk(and_3_out));
  // Probe on Y
  // Probe on shifter_1_p5
  // Probe on shifter_1_p6
  // Probe on shifter_1_p7
  // Probe on shifter_1_p8
  // Probe on shifter_1_p9
  // Probe on shifter_1_p10
  // Probe on shifter_1_p11
  Comparator #(.Bits(64)) comparator_5 (.a(shifter_1_p7), .b({64{1'b0}}), .eq(comparator_5_eq));  // open: gt, lt

  // Notes on the sheet:
  //   C: Hz: 2000
endmodule
