// Digital circuit day23_merger.dig as structural Verilog
module day23_merger (
  input  C,
  input  in1_en,
  input  [63:0] in1_val,
  input  in2_en,
  input  [63:0] in2_val,
  output out_en,
  output [63:0] out_val,
  output out_busy
);

  wire and_1_out, and_2_out, and_3_out, and_4_out, decoder_1_out_0, decoder_1_out_1, decoder_1_out_2,
       fifo_1_out_avail, fifo_2_out_avail, multiplexer_1_out, not_1_out, src_q;
  wire [1:0] phase_out;
  wire [63:0] fifo_1_out_val, fifo_2_out_val;

  fifo fifo_1 (
    .C(C), .in_en(in1_en), .in_val(in1_val), .out_en(and_2_out), .out_avail(fifo_1_out_avail),
    .out_val(fifo_1_out_val));  // open: cnt
  fifo fifo_2 (
    .C(C), .in_en(in2_en), .in_val(in2_val), .out_en(and_1_out), .out_avail(fifo_2_out_avail),
    .out_val(fifo_2_out_val));  // open: cnt
  or or_1 (out_en, and_2_out, and_1_out);
  and and_1 (and_1_out, multiplexer_1_out, fifo_2_out_avail);
  and and_2 (and_2_out, fifo_1_out_avail, not_1_out);
  and and_3 (and_3_out, out_en, decoder_1_out_2);
  and and_4 (and_4_out, ~fifo_1_out_avail, fifo_2_out_avail);  // And
  Counter #(.Bits(2)) phase (.en(out_en), .C(C), .clr(and_3_out), .out(phase_out));  // open: ovf
  // Probe on phase_out
  Decoder #(.Selector_Bits(2)) decoder_1 (
    .sel(phase_out), .out_0(decoder_1_out_0), .out_1(decoder_1_out_1), .out_2(decoder_1_out_2));  // open: out_3
  Register src (.D(and_4_out), .C(C), .en(decoder_1_out_0), .Q(src_q));
  Multiplexer multiplexer_1 (.sel(decoder_1_out_0), .in_0(src_q), .in_1(and_4_out), .out(multiplexer_1_out));
  or or_2 (out_busy, decoder_1_out_1, fifo_1_out_avail, fifo_2_out_avail, decoder_1_out_2);
  not not_1 (not_1_out, multiplexer_1_out);
  Multiplexer #(.Bits(64)) multiplexer_2 (
    .sel(multiplexer_1_out), .in_0(fifo_1_out_val), .in_1(fifo_2_out_val), .out(out_val));

  // Notes on the sheet:
  //   in1_val: default 6
  //   in2_val: default 6
endmodule
