// Digital circuit day23_merger_test.dig as structural Verilog
module day23_merger_test (
  input  C
);

  wire comparator_1_gt, comparator_2_gt, counter_1_ovf, counter_2_ovf, day23_merger_1_out_busy,
       day23_merger_1_out_en, shifter_1_p4, shifter_1_p5, shifter_1_p6, shifter_1_p7, shifter_1_p8,
       shifter_1_p9, shifter_1_p10, shifter_2_p2, shifter_2_p4, shifter_2_p5, shifter_2_p6, shifter_2_p7,
       shifter_2_p8, shifter_2_p9, shifter_2_p10, shifter_3_p2, shifter_3_p4, shifter_3_p5, shifter_3_p6,
       shifter_3_p7, shifter_3_p8, shifter_3_p9, shifter_3_p10, shifter_3_p11;
  wire [7:0] counter_1_out, counter_2_out, input_2_d, input_d;
  wire [63:0] day23_merger_1_out_val;

  Counter #(.Bits(8)) counter_1 (.en(1'b1), .C(C), .clr(1'b0), .out(counter_1_out), .ovf(counter_1_ovf));
  Counter #(.Bits(8)) counter_2 (.en(1'b1), .C(C), .clr(1'b0), .out(counter_2_out), .ovf(counter_2_ovf));
  Break break_1 (.brk(counter_1_ovf));
  Break break_2 (.brk(counter_2_ovf));
  ROM #(.AddrBits(8), .Bits(8)) \input  (.A(counter_1_out), .sel(1'b1), .D(input_d));
  ROM #(.AddrBits(8), .Bits(8)) input_2 (.A(counter_2_out), .sel(1'b1), .D(input_2_d));
  Comparator #(.Bits(8)) comparator_1 (.a(input_d), .b({8{1'b0}}), .gt(comparator_1_gt));  // open: eq, lt
  Comparator #(.Bits(8)) comparator_2 (.a(input_2_d), .b({8{1'b0}}), .gt(comparator_2_gt));  // open: eq, lt
  day23_merger day23_merger_1 (
    .C(C), .in1_en(comparator_1_gt), .in1_val({{56{1'b0}}, input_d}), .in2_en(comparator_2_gt),
    .in2_val({{56{1'b0}}, input_2_d}), .out_en(day23_merger_1_out_en), .out_val(day23_merger_1_out_val),
    .out_busy(day23_merger_1_out_busy));
  // Probe on day23_merger_1_out_busy
  // shifter shifter_1: pin names not known; wires that end beside it: day23_merger_1_out_en, day23_merger_1_out_val, C, shifter_1_p4, shifter_1_p5, shifter_1_p6, shifter_1_p7, shifter_1_p8, shifter_1_p9, shifter_1_p10
  // shifter shifter_2: pin names not known; wires that end beside it: day23_merger_1_out_en, shifter_2_p2, C, shifter_2_p4, shifter_2_p5, shifter_2_p6, shifter_2_p7, shifter_2_p8, shifter_2_p9, shifter_2_p10
  // shifter shifter_3: pin names not known; wires that end beside it: day23_merger_1_out_en, shifter_3_p2, C, shifter_3_p4, shifter_3_p5, shifter_3_p6, shifter_3_p7, shifter_3_p8, shifter_3_p9, shifter_3_p10, shifter_3_p11
  // Probe on shifter_1_p4
  // Probe on shifter_1_p5
  // Probe on shifter_1_p6
  // Probe on shifter_1_p7
  // Probe on shifter_1_p8
  // Probe on shifter_1_p9
  // Probe on shifter_1_p10
  // Probe on shifter_2_p2
  // Probe on shifter_2_p4
  // Probe on shifter_2_p5
  // Probe on shifter_2_p6
  // Probe on shifter_2_p7
  // Probe on shifter_2_p8
  // Probe on shifter_2_p9
  // Probe on shifter_2_p10
  // Probe on shifter_3_p2
  // Probe on shifter_3_p4
  // Probe on shifter_3_p5
  // Probe on shifter_3_p6
  // Probe on shifter_3_p7
  // Probe on shifter_3_p8
  // Probe on shifter_3_p9
  // Probe on shifter_3_p10
  // Probe on shifter_3_p11

  // Notes on the sheet:
  //   contents of input (hex, n*v repeats v):
  //   11,12,0,13,e,0,0,f,10,0,0,0,0,0,0,0,0,0,0,0,0,0,0,0,31,0,0,0,0,0,0,32,0,0,0,33
  //   contents of input_2 (hex, n*v repeats v):
  //   0,0,0,0,0,21,22,23
endmodule
