// Digital circuit day23_node.dig as structural Verilog
module day23_node (
  input  C,
  input  in_en,
  input  [63:0] in_val,
  input  [63:0] addr,
  input  in_busy,
  output out_en,
  output [63:0] out_val,
  output [63:0] addr_next,
  output [31:0] out_cnt,
  output out_busy
);

  wire day23_merger_1_out_busy, day23_parser_1_nextout_en, day23_parser_1_out_en, fifo_preloaded_1_out_avail,
       fifo_preloaded_2_out_avail, intcode_1_in_req, intcode_1_out_en, intcode_1_running, intcode_1_write_en,
       not_1_out;
  wire [1:0] intcode_1_phase;
  wire [15:0] intcode_1_pc, intcode_1_rw_addr;
  wire [63:0] day23_parser_1_nextout_val, day23_parser_1_out_val, fifo_preloaded_1_out_val,
       fifo_preloaded_2_out_val, intcode_1_instr, intcode_1_out_val, intcode_1_write_val;

  Add #(.Bits(64)) add_1 (.a(addr), .b(64'h1), .c_i(1'b0), .s(addr_next));  // open: c_o
  day23_parser day23_parser_1 (
    .in_en(in_en), .in_val(in_val), .address(addr), .C(C), .out_en(day23_parser_1_out_en),
    .out_val(day23_parser_1_out_val), .nextout_en(day23_parser_1_nextout_en),
    .nextout_val(day23_parser_1_nextout_val));  // open: out_y
  fifo_preloaded fifo_preloaded_1 (
    .C(C), .\initial ({64{1'b1}}), .in_en(day23_parser_1_out_en), .in_val(day23_parser_1_out_val),
    .out_en(fifo_preloaded_1_out_avail), .out_avail(fifo_preloaded_1_out_avail),
    .out_val(fifo_preloaded_1_out_val));  // open: cnt
  fifo_preloaded fifo_preloaded_2 (
    .C(C), .\initial (addr), .in_en(fifo_preloaded_1_out_avail), .in_val(fifo_preloaded_1_out_val),
    .out_en(intcode_1_in_req), .out_avail(fifo_preloaded_2_out_avail), .out_val(fifo_preloaded_2_out_val));  // open: cnt
  intcode #(.generic("ramLabel := \"ram\" + args.label;")) intcode_1 (
    .clock(C), .in_val(fifo_preloaded_2_out_val), .in_avail(fifo_preloaded_2_out_avail),
    .write_val(intcode_1_write_val), .rw_addr(intcode_1_rw_addr), .write_en(intcode_1_write_en),
    .pc(intcode_1_pc), .instr(intcode_1_instr), .phase(intcode_1_phase), .out_en(intcode_1_out_en),
    .out_val(intcode_1_out_val), .running(intcode_1_running), .in_req(intcode_1_in_req));  // open: X, Y, r, cycle_cnt
  Break in (.brk(intcode_1_in_req));
  // Probe instr on intcode_1_instr
  not not_1 (not_1_out, intcode_1_running);
  // Probe write_en on intcode_1_write_en
  // Probe pc on intcode_1_pc
  Break halt (.brk(not_1_out));
  // Probe w_val on intcode_1_write_val
  // Probe addr on intcode_1_rw_addr
  // Probe phase on intcode_1_phase
  Counter #(.Bits(32)) counter_1 (.en(intcode_1_out_en), .C(C), .clr(1'b0));  // open: out, ovf
  day23_merger day23_merger_1 (
    .C(C), .in1_en(intcode_1_out_en), .in1_val(intcode_1_out_val), .in2_en(day23_parser_1_nextout_en),
    .in2_val(day23_parser_1_nextout_val), .out_en(out_en), .out_val(out_val),
    .out_busy(day23_merger_1_out_busy));
  or or_1 (out_cnt[0], ~intcode_1_in_req, intcode_1_out_en, fifo_preloaded_2_out_avail, day23_merger_1_out_busy);  // Or
  or or_2 (out_busy, in_busy, out_cnt[0]);
  // Pins of 1 and 32 bits meet at out_cnt
endmodule
