// Digital circuit day23_parser.dig as structural Verilog
module day23_parser (
  input  in_en,
  input  [63:0] in_val,
  input  [63:0] address,
  input  C,
  output out_en,
  output [63:0] out_val,
  output nextout_en,
  output [63:0] nextout_val,
  output out_y
);

  wire addr_matched_q, and_1_out, and_2_out, and_3_out, and_4_out, comparator_1_eq, decoder_1_out_0,
       decoder_1_out_1, or_2_out;
  wire [1:0] phase_out;

  Comparator #(.Bits(64)) comparator_1 (.a(address), .b(in_val), .eq(comparator_1_eq));  // open: gt, lt
  and and_1 (and_1_out, in_en, out_y);
  Counter #(.Bits(2)) phase (.en(in_en), .C(C), .clr(and_1_out), .out(phase_out));  // open: ovf
  Decoder #(.Selector_Bits(2)) decoder_1 (
    .sel(phase_out), .out_0(decoder_1_out_0), .out_1(decoder_1_out_1), .out_2(out_y));  // open: out_3
  and and_2 (and_2_out, decoder_1_out_0, ~comparator_1_eq, in_en);  // And
  or or_1 (nextout_en, and_4_out, and_2_out);
  and and_3 (and_3_out, in_en, decoder_1_out_0);
  or or_2 (or_2_out, decoder_1_out_1, out_y);
  Register addr_matched (.D(comparator_1_eq), .C(C), .en(and_3_out), .Q(addr_matched_q));
  and and_4 (and_4_out, or_2_out, ~addr_matched_q, in_en);  // And
  // Probe on addr_matched_q
  and and_5 (out_en, addr_matched_q, in_en, or_2_out);

  assign nextout_val = in_val;
  assign out_val = in_val;

  // Notes on the sheet:
  //   in_val: default 6
  //   address: default 6
  //   out_y: Is this the Y value ?
endmodule

/* Test case test:
C address in_en in_val out_en out_val
0 0       0     0      0      0

# no input
0 6       0     2      0      X
1 6       0     2      X      X

# non-matching address
0 6       1     3      0      X
1 6       1     3      X      X
0 6       1     4      0      X
1 6       1     4      X      X
0 6       1     5      0      X
1 6       1     5      X      X

# matching address
0 6       1     6      0      X
1 6       1     6      X      X
0 6       1     7      1      7
1 6       1     7      X      X
0 6       1     8      1      8
1 6       1     8      X      X

0 6       0     2      0      X
*/
