// Digital circuit day23_parser_test.dig as structural Verilog
module day23_parser_test (
  input  C
);

  wire comparator_1_lt, counter_1_ovf, day23_parser_1_nextout_en, day23_parser_1_out_en,
       day23_parser_1_out_y, day23_parser_2_nextout_en, day23_parser_2_out_en, day23_parser_2_out_y,
       demultiplexer_1_out_0, demultiplexer_1_out_1, shifter_1_out_0, shifter_1_out_1, shifter_1_out_2,
       shifter_1_out_3, shifter_1_out_4, shifter_1_out_5, shifter_1_out_6, shifter_1_out_7, shifter_2_p4,
       shifter_2_p5, shifter_2_p6, shifter_2_p7, shifter_2_p8, shifter_2_p9, shifter_2_p10, shifter_3_p2,
       shifter_3_p4, shifter_3_p5, shifter_3_p6, shifter_3_p7, shifter_3_p8, shifter_3_p9, shifter_3_p10,
       shifter_3_p11, shifter_4_p4, shifter_4_p5, shifter_4_p6, shifter_4_p7, shifter_4_p8, shifter_4_p9,
       shifter_4_p10, shifter_5_p2, shifter_5_p4, shifter_5_p5, shifter_5_p6, shifter_5_p7, shifter_5_p8,
       shifter_5_p9, shifter_5_p10, shifter_5_p11, shifter_6_out_0, shifter_6_out_1, shifter_6_out_2,
       shifter_6_out_3, shifter_6_out_4, shifter_6_out_5, shifter_6_out_6, shifter_6_out_7;
  wire [4:0] counter_1_out;
  wire [7:0] input_d;
  wire [63:0] day23_parser_1_nextout_val, day23_parser_1_out_val, day23_parser_2_nextout_val,
       day23_parser_2_out_val;

  Counter #(.Bits(5)) counter_1 (.en(1'b1), .C(C), .clr(1'b0), .out(counter_1_out), .ovf(counter_1_ovf));
  Break break_1 (.brk(counter_1_ovf));
  ROM #(.AddrBits(5), .Bits(8)) \input  (.A(counter_1_out), .sel(1'b1), .D(input_d));
  Comparator #(.Bits(8)) comparator_1 (.a({8{1'b0}}), .b(input_d), .lt(comparator_1_lt));  // open: gt, eq
  day23_parser day23_parser_1 (
    .in_en(comparator_1_lt), .in_val({{56{1'b0}}, input_d}), .address(64'h73), .C(C),
    .out_en(day23_parser_1_out_en), .out_val(day23_parser_1_out_val), .nextout_en(day23_parser_1_nextout_en),
    .nextout_val(day23_parser_1_nextout_val), .out_y(day23_parser_1_out_y));
  day23_parser day23_parser_2 (
    .in_en(day23_parser_1_nextout_en), .in_val(day23_parser_1_nextout_val), .address(64'h74), .C(C),
    .out_en(day23_parser_2_out_en), .out_val(day23_parser_2_out_val), .nextout_en(day23_parser_2_nextout_en),
    .nextout_val(day23_parser_2_nextout_val), .out_y(day23_parser_2_out_y));
  // Probe on day23_parser_2_out_y
  Demultiplexer demultiplexer_1 (
    .sel(day23_parser_1_out_y), .in(day23_parser_1_out_en), .out_0(demultiplexer_1_out_0),
    .out_1(demultiplexer_1_out_1));
  shifter shifter_1 (
    .in_en(demultiplexer_1_out_0), .in_val(day23_parser_1_out_val), .C(C), .out_0(shifter_1_out_0),
    .out_1(shifter_1_out_1), .out_2(shifter_1_out_2), .out_3(shifter_1_out_3), .out_4(shifter_1_out_4),
    .out_5(shifter_1_out_5), .out_6(shifter_1_out_6), .out_7(shifter_1_out_7));
  // shifter shifter_2: pin names not known; wires that end beside it: day23_parser_2_out_en, day23_parser_2_out_val, C, shifter_2_p4, shifter_2_p5, shifter_2_p6, shifter_2_p7, shifter_2_p8, shifter_2_p9, shifter_2_p10
  // shifter shifter_3: pin names not known; wires that end beside it: day23_parser_2_out_en, shifter_3_p2, C, shifter_3_p4, shifter_3_p5, shifter_3_p6, shifter_3_p7, shifter_3_p8, shifter_3_p9, shifter_3_p10, shifter_3_p11
  // shifter shifter_4: pin names not known; wires that end beside it: day23_parser_2_nextout_en, day23_parser_2_nextout_val, C, shifter_4_p4, shifter_4_p5, shifter_4_p6, shifter_4_p7, shifter_4_p8, shifter_4_p9, shifter_4_p10
  // shifter shifter_5: pin names not known; wires that end beside it: day23_parser_2_nextout_en, shifter_5_p2, C, shifter_5_p4, shifter_5_p5, shifter_5_p6, shifter_5_p7, shifter_5_p8, shifter_5_p9, shifter_5_p10, shifter_5_p11
  // Probe on shifter_1_out_0
  // Probe on shifter_1_out_1
  // Probe on shifter_1_out_2
  // Probe on shifter_1_out_3
  // Probe on shifter_1_out_4
  // Probe on shifter_1_out_5
  // Probe on shifter_1_out_6
  // Probe on shifter_1_out_7
  // Probe on shifter_2_p4
  // Probe on shifter_2_p5
  // Probe on shifter_2_p6
  // Probe on shifter_2_p7
  // Probe on shifter_2_p8
  // Probe on shifter_2_p9
  // Probe on shifter_2_p10
  // Probe on shifter_3_p2
  // Probe on shifter_3_p4
  // Probe on shifter_3_p5
  // Probe on shifter_3_p6
  // Probe on shifter_3_p7
  // Probe on shifter_3_p8
  // Probe on shifter_3_p9
  // Probe on shifter_3_p10
  // Probe on shifter_3_p11
  // Probe on shifter_4_p4
  // Probe on shifter_4_p5
  // Probe on shifter_4_p6
  // Probe on shifter_4_p7
  // Probe on shifter_4_p8
  // Probe on shifter_4_p9
  // Probe on shifter_4_p10
  // Probe on shifter_5_p2
  // Probe on shifter_5_p4
  // Probe on shifter_5_p5
  // Probe on shifter_5_p6
  // Probe on shifter_5_p7
  // Probe on shifter_5_p8
  // Probe on shifter_5_p9
  // Probe on shifter_5_p10
  // Probe on shifter_5_p11
  shifter shifter_6 (
    .in_en(demultiplexer_1_out_1), .in_val(day23_parser_1_out_val), .C(C), .out_0(shifter_6_out_0),
    .out_1(shifter_6_out_1), .out_2(shifter_6_out_2), .out_3(shifter_6_out_3), .out_4(shifter_6_out_4),
    .out_5(shifter_6_out_5), .out_6(shifter_6_out_6), .out_7(shifter_6_out_7));
  // Probe on shifter_6_out_0
  // Probe on shifter_6_out_1
  // Probe on shifter_6_out_2
  // Probe on shifter_6_out_3
  // Probe on shifter_6_out_4
  // Probe on shifter_6_out_5
  // Probe on shifter_6_out_6
  // Probe on shifter_6_out_7

  // Notes on the sheet:
  //   contents of input (hex, n*v repeats v):
  //   1,2,3,0,0,0,73,0,41,0,0,0,0,42,74,50,51,2,0,0,3,0,0,4,0,0,73,43,44
endmodule
