// Digital circuit day25.dig as structural Verilog
module day25 (
  input  C,
  output [15:0] in_cnt
);

  wire intcode_1_p3, intcode_1_p4, intcode_1_p5, intcode_1_p6, intcode_1_p7, not_1_out;
  wire [7:0] input_d;

  Counter #(.Bits(16)) counter_1 (.en(intcode_1_p3), .C(C), .clr(1'b0), .out(in_cnt));  // open: ovf
  ROM #(.AddrBits(16), .Bits(8)) \input  (.A(in_cnt), .sel(1'b1), .D(input_d));
  // intcode #(.generic("ramLabel := \"ram\";")) intcode_1: pin names not known; wires that end beside it: C, {{56{1'b0}}, input_d}, intcode_1_p3, intcode_1_p4, intcode_1_p5, intcode_1_p6, intcode_1_p7, intcode_1_p3
  not not_1 (not_1_out, intcode_1_p7);
  // Probe on intcode_1_p6
  Break in_req (.brk(intcode_1_p3));
  Terminal #(.termWidth(130)) terminal_1 (.D(intcode_1_p5), .C(C), .en(intcode_1_p4));
  Break #(.Cycles(10000000)) halt (.brk(not_1_out));

  // Notes on the sheet:
  //   C: Hz: 100000
  //   contents of input (hex, n*v repeats v):
  //   73,6f,75,74,68,a,73,6f,75,74,68,a,6e,6f,72,74,68,a,65,61,73,74,a,6e,6f,72,74,68,a,
  //   73,6f,75,74,68,a,77,65,73,74,a,6e,6f,72,74,68,a,77,65,73,74,a,74,61,6b,65,20,6d,75,
  //   67,a,6e,6f,72,74,68,a,73,6f,75,74,68,a,77,65,73,74,a,65,61,73,74,a,65,61,73,74,a,
  //   65,61,73,74,a,74,61,6b,65,20,63,6f,69,6e,a,6e,6f,72,74,68,a,65,61,73,74,a,77,65,73,
  //   74,a,6e,6f,72,74,68,a,74,61,6b,65,20,68,79,70,65,72,63,75,62,65,a,73,6f,75,74,68,
  //   a,73,6f,75,74,68,a,73,6f,75,74,68,a,65,61,73,74,a,77,65,73,74,a,77,65,73,74,a,74,
  //   61,6b,65,20,61,73,74,72,6f,6c,61,62,65,a,6e,6f,72,74,68,a,65,61,73,74,a,6e,6f,72,
  //   74,68,a,69,6e,76,a,65,61,73,74,a,69,6e,76,a
endmodule
