// Digital circuit day25_inlined.dig as structural Verilog
module day25_inlined (
  input  clock,
  input  [63:0] in_val,
  input  in_avail,
  output [63:0] write_val,
  output [15:0] rw_addr,
  output write_en,
  output [15:0] pc,
  output [63:0] X,
  output [63:0] Y,
  output [63:0] r,
  output [63:0] instr,
  output [1:0] phase,
  output out_en,
  output [63:0] out_val,
  output [31:0] cycle_cnt,
  output running,
  output in_req,
  output [15:0] relbase,
  output [15:0] in_cnt
);

  wire addbase, advance, and_3_out, and_4_out, and_8_out, and_9_out, and_10_out, and_11_out, and_12_out,
       and_13_out, and_14_out, and_17_out, badinstr, C, C_t, comparator_1_eq, comparator_2_gt,
       decoder_1_out_3, decoder_1_out_4, decoder_1_out_5, decoder_1_out_6, decoder_1_out_9, decoder_2_out_1,
       decoder_2_out_2, decoder_2_out_3, decoder_3_out_1, decoder_3_out_2, decoder_3_out_3, decoder_3_out_4,
       decoder_3_out_5, decoder_3_out_6, decoder_3_out_7, decoder_3_out_8, decoder_3_out_9, decoder_4_out_1,
       decoder_5_out_3, decoder_5_out_4, decoder_6_out_1, decoder_6_out_3, decoder_7_out_0, decoder_7_out_1,
       decoder_7_out_2, decoder_7_out_3, decoder_8_out_5, decoder_8_out_6, decoder_9_out_0, decoder_9_out_1,
       decoder_9_out_2, decoder_10_out_9, indirect, jump, next, nor_1_out, nor_2_out, not_1_out, or_1_out,
       or_2_out, or_3_out, or_6_out, or_7_out, run_nq, sub_1_c_o, sub_2_c_o, sub_3_c_o, sub_4_c_o, sub_5_c_o;
  wire [0:0] lt_eq, lt_lt;
  wire [3:0] opcode;
  wire [15:0] add_1_s, add_3_s, add_4_s, instr_addr, multiplexer_1_out, multiplexer_2_out, multiplexer_4_out,
       param_addr;
  wire [63:0] mul64_mul, multiplexer_5_out, multiplexer_7_out, multiplexer_8_out, multiplexer_9_out,
       multiplexer_10_out, plus_s, sub_1_s, sub_2_s, sub_3_s, sub_4_s, sub_5_s;

  Counter #(.Bits(32)) u_cycle_cnt (.en(running), .C(C_t), .clr(1'b0), .out(cycle_cnt));  // open: ovf
  T_FF #(.Default(1)) run (.T(badinstr), .C(C_t), .Q(running), .nQ(run_nq));
  Break halt (.brk(run_nq));
  nand nand_1 (C, running, clock);
  Decoder #(.Selector_Bits(4)) decoder_1 (
    .sel(opcode), .out_3(decoder_1_out_3), .out_4(decoder_1_out_4), .out_5(decoder_1_out_5),
    .out_6(decoder_1_out_6), .out_9(decoder_1_out_9));  // open: out_0, out_1, out_2, out_7, out_8, out_10, out_11, out_12, out_13, out_14, out_15
  Decoder #(.Selector_Bits(2)) decoder_2 (
    .sel(phase), .out_1(decoder_2_out_1), .out_2(decoder_2_out_2), .out_3(decoder_2_out_3));  // open: out_0
  and and_1 (C_t, running, clock);
  Add #(.Bits(16)) add_1 (.a(out_val[15:0]), .b(relbase), .c_i(1'b0), .s(add_1_s));  // open: c_o
  Multiplexer #(.Bits(16)) multiplexer_1 (.sel(addbase), .in_0(out_val[15:0]), .in_1(add_1_s), .out(multiplexer_1_out));
  Decoder #(.Selector_Bits(4)) decoder_3 (
    .sel(opcode), .out_1(decoder_3_out_1), .out_2(decoder_3_out_2), .out_3(decoder_3_out_3),
    .out_4(decoder_3_out_4), .out_5(decoder_3_out_5), .out_6(decoder_3_out_6), .out_7(decoder_3_out_7),
    .out_8(decoder_3_out_8), .out_9(decoder_3_out_9));  // open: out_0, out_10, out_11, out_12, out_13, out_14, out_15
  Decoder #(.Selector_Bits(2)) decoder_4 (.sel(phase), .out_1(decoder_4_out_1));  // open: out_0, out_2, out_3
  Multiplexer #(.Bits(16)) multiplexer_2 (
    .sel(indirect), .in_0(instr_addr), .in_1(multiplexer_1_out), .out(multiplexer_2_out));
  Register #(.Bits(16)) u_param_addr (.D(multiplexer_2_out), .C(C), .en(1'b1), .Q(param_addr));
  RAMDualPort #(.AddrBits(16), .isProgramMemory("true"), .Bits(64), .generic("this.Label=args.ramLabel;")) ram (
    .A(rw_addr), .Din(write_val), .str(write_en), .C(C_t), .ld(1'b1), .D(out_val));
  or or_1 (or_1_out, decoder_1_out_3, decoder_1_out_4, decoder_1_out_9);
  or or_2 (or_2_out, decoder_1_out_5, decoder_1_out_6);
  Counter #(.Bits(16)) counter_1 (.en(in_avail), .C(C_t), .clr(1'b0), .out(in_cnt));  // open: ovf
  nor nor_1 (nor_1_out, decoder_3_out_1, decoder_3_out_2, decoder_3_out_3, decoder_3_out_4, decoder_3_out_5, decoder_3_out_6, decoder_3_out_7, decoder_3_out_8, decoder_3_out_9);
  and and_2 (badinstr, nor_1_out, decoder_4_out_1);
  and and_3 (and_3_out, or_1_out, decoder_2_out_1);
  and and_4 (and_4_out, or_2_out, decoder_2_out_2);
  ROM #(.AddrBits(16), .Bits(8)) \input  (.A(in_cnt), .sel(1'b1), .D(in_val[7:0]));
  Multiplexer #(.Bits(16)) multiplexer_3 (.sel(C_t), .in_0(param_addr), .in_1(instr_addr), .out(rw_addr));
  Add #(.Bits(16)) add_2 (.a({{14{1'b0}}, phase}), .b(pc), .c_i(1'b0), .s(instr_addr));  // open: c_o
  or or_3 (or_3_out, and_3_out, and_4_out, decoder_2_out_3);
  Add #(.Bits(16)) add_3 (.a(pc), .b({{14{1'b0}}, phase}), .c_i(1'b1), .s(add_3_s));  // open: c_o
  and and_5 (next, advance, or_3_out);
  not not_1 (not_1_out, running);
  Multiplexer #(.Bits(16)) multiplexer_4 (.sel(jump), .in_0(add_3_s), .in_1(out_val[15:0]), .out(multiplexer_4_out));
  // Probe on cycle_cnt
  Break u_in_req (.brk(in_avail));
  Register #(.Bits(16)) u_pc (.D(multiplexer_4_out), .C(C_t), .en(next), .Q(pc));
  Terminal terminal_1 (.D(out_val), .C(C_t), .en(out_en));
  Break #(.Cycles(10000000)) halt_2 (.brk(not_1_out));
  Counter #(.Bits(2)) u_phase (.en(advance), .C(C_t), .clr(next), .out(phase));  // open: ovf
  nand nand_2 (advance, in_avail, ~in_avail);  // NAnd
  Decoder #(.Selector_Bits(4)) decoder_5 (
    .sel(opcode), .out_3(decoder_5_out_3), .out_4(decoder_5_out_4));  // open: out_0, out_1, out_2, out_5, out_6, out_7, out_8, out_9, out_10, out_11, out_12, out_13, out_14, out_15
  Decoder #(.Selector_Bits(2)) decoder_6 (
    .sel(phase), .out_1(decoder_6_out_1), .out_3(decoder_6_out_3));  // open: out_0, out_2
  Decoder #(.Selector_Bits(2)) decoder_7 (
    .sel(phase), .out_0(decoder_7_out_0), .out_1(decoder_7_out_1), .out_2(decoder_7_out_2),
    .out_3(decoder_7_out_3));
  Decoder #(.Selector_Bits(4)) decoder_8 (
    .sel(opcode), .out_5(decoder_8_out_5), .out_6(decoder_8_out_6));  // open: out_0, out_1, out_2, out_3, out_4, out_7, out_8, out_9, out_10, out_11, out_12, out_13, out_14, out_15
  and and_6 (out_en, decoder_5_out_4, decoder_6_out_1);
  and and_7 (in_avail, decoder_5_out_3, decoder_6_out_1);
  Sub #(.Bits(64)) sub_1 (.a(instr), .b(64'h4e20), .c_i(1'b0), .s(sub_1_s), .c_o(sub_1_c_o));
  Comparator #(.Signed("true"), .Bits(64)) comparator_1 (.a({64{1'b0}}), .b(X), .eq(comparator_1_eq));  // open: gt, lt
  Multiplexer #(.Bits(64)) multiplexer_5 (.sel(sub_1_c_o), .in_0(sub_1_s), .in_1(instr), .out(multiplexer_5_out));
  and and_8 (and_8_out, ~sub_1_c_o, decoder_7_out_3);  // And
  and and_9 (and_9_out, ~comparator_1_eq, decoder_8_out_5);  // And
  and and_10 (and_10_out, comparator_1_eq, decoder_8_out_6);
  Multiplexer #(.Bits(64)) multiplexer_6 (.sel(in_avail), .in_0(r), .in_1(in_val), .out(write_val));
  or or_4 (jump, and_9_out, and_10_out);
  or or_5 (write_en, in_avail, decoder_6_out_3);
  Sub #(.Bits(64)) sub_2 (.a(multiplexer_5_out), .b(64'h7d0), .c_i(1'b0), .s(sub_2_s), .c_o(sub_2_c_o));
  Sub #(.Bits(64)) sub_3 (.a(multiplexer_7_out), .b(64'h3e8), .c_i(1'b0), .s(sub_3_s), .c_o(sub_3_c_o));
  Multiplexer #(.Bits(64)) multiplexer_7 (
    .sel(sub_2_c_o), .in_0(sub_2_s), .in_1(multiplexer_5_out), .out(multiplexer_7_out));
  Multiplexer #(.Bits(64)) multiplexer_8 (
    .sel(sub_3_c_o), .in_0(sub_3_s), .in_1(multiplexer_7_out), .out(multiplexer_8_out));
  and and_11 (and_11_out, ~sub_3_c_o, decoder_7_out_2);  // And
  and and_12 (and_12_out, ~sub_2_c_o, decoder_7_out_2);  // And
  Decoder #(.Selector_Bits(2)) decoder_9 (
    .sel(phase), .out_0(decoder_9_out_0), .out_1(decoder_9_out_1), .out_2(decoder_9_out_2));  // open: out_3
  Sub #(.Bits(64)) sub_4 (.a(multiplexer_8_out), .b(64'hc8), .c_i(1'b0), .s(sub_4_s), .c_o(sub_4_c_o));
  Sub #(.Bits(64)) sub_5 (.a(multiplexer_9_out), .b(64'h64), .c_i(1'b0), .s(sub_5_s), .c_o(sub_5_c_o));
  Register #(.Bits(64)) u_instr (.D(out_val), .C(C_t), .en(decoder_9_out_0), .Q(instr));
  Multiplexer #(.Bits(64)) multiplexer_9 (
    .sel(sub_4_c_o), .in_0(sub_4_s), .in_1(multiplexer_8_out), .out(multiplexer_9_out));
  Multiplexer #(.Bits(64)) multiplexer_10 (
    .sel(sub_5_c_o), .in_0(sub_5_s), .in_1(multiplexer_9_out), .out(multiplexer_10_out));
  and and_13 (and_13_out, ~sub_5_c_o, decoder_7_out_1);  // And
  and and_14 (and_14_out, ~sub_4_c_o, decoder_7_out_1);  // And
  Comparator #(.Bits(64)) comparator_2 (.a(multiplexer_10_out), .b(64'h9), .gt(comparator_2_gt));  // open: eq, lt
  or or_6 (or_6_out, and_8_out, and_12_out, and_14_out);
  Register #(.Bits(64)) u_X (.D(out_val), .C(C_t), .en(decoder_9_out_1), .Q(X));
  Add #(.Bits(64)) plus (.a(X), .b(Y), .c_i(1'b0), .s(plus_s));  // open: c_o
  Comparator #(.Signed("true"), .Bits(64)) lt (.a(X), .b(Y), .eq(lt_eq[0]), .lt(lt_lt[0]));  // open: gt
  nor nor_2 (nor_2_out, and_11_out, and_13_out);
  mul64 mul64 (.a(X), .b(Y), .mul(mul64_mul));
  Multiplexer #(.Bits(4)) multiplexer_11 (
    .sel(comparator_2_gt), .in_0(multiplexer_10_out[3:0]), .in_1(4'b1111), .out(opcode));
  or or_7 (or_7_out, nor_2_out, or_6_out);
  and and_15 (addbase, or_6_out, ~decoder_7_out_0);  // And
  and and_16 (indirect, or_7_out, ~decoder_7_out_0);  // And
  Register #(.Bits(64)) u_Y (.D(out_val), .C(C_t), .en(decoder_9_out_2), .Q(Y));
  Multiplexer #(.Selector_Bits(4), .Bits(64)) multiplexer_12 (
    .sel(opcode), .in_0({64{1'b0}}), .in_1(plus_s), .in_2(mul64_mul), .in_3({64{1'b0}}), .in_4({64{1'b0}}),
    .in_5({64{1'b0}}), .in_6({64{1'b0}}), .in_7({{63{1'b0}}, lt_lt[0]}), .in_8({{63{1'b0}}, lt_eq[0]}),
    .in_9({64{1'b0}}), .in_10({64{1'b0}}), .in_11({64{1'b0}}), .in_12({64{1'b0}}), .in_13({64{1'b0}}),
    .in_14({64{1'b0}}), .in_15({64{1'b0}}), .out(r));
  and and_17 (and_17_out, decoder_10_out_9, decoder_9_out_1);
  Decoder #(.Selector_Bits(4)) decoder_10 (
    .sel(opcode), .out_9(decoder_10_out_9));  // open: out_0, out_1, out_2, out_3, out_4, out_5, out_6, out_7, out_8, out_10, out_11, out_12, out_13, out_14, out_15
  Add #(.Bits(16)) add_4 (.a(relbase), .b(out_val[15:0]), .c_i(1'b0), .s(add_4_s));  // open: c_o
  Register #(.Bits(16)) u_relbase (.D(add_4_s), .C(C_t), .en(and_17_out), .Q(relbase));

  assign in_req = in_avail;
  // also tied to GND on the sheet: {in_val[8], in_val[9], in_val[10], in_val[11], in_val[12], in_val[13], in_val[14], in_val[15], in_val[16], in_val[17], in_val[18], in_val[19], in_val[20], in_val[21], in_val[22], in_val[23], in_val[24], in_val[25], in_val[26], in_val[27], in_val[28], in_val[29], in_val[30], in_val[31], in_val[32], in_val[33], in_val[34], in_val[35], in_val[36], in_val[37], in_val[38], in_val[39], in_val[40], in_val[41], in_val[42], in_val[43], in_val[44], in_val[45], in_val[46], in_val[47], in_val[48], in_val[49], in_val[50], in_val[51], in_val[52], in_val[53], in_val[54], in_val[55], in_val[56], in_val[57], in_val[58], in_val[59], in_val[60], in_val[61], in_val[62], in_val[63]}

  // Other names for the same wires on the sheet: ram_addr[15:0] = rw_addr; ram_rval[63:0] = out_val;
  //   ram_we = write_en; ram_wval[63:0] = write_val

  // Notes on the sheet:
  //   clock: Hz: 20000
  //   Clock
  //   Instruction complete
  //   Param addr
  //   Pins
  //   Bad instruction detection
  //   RAM
  //   Instr/Param addr
  //   contents of input (hex, n*v repeats v):
  //   73,6f,75,74,68,a,73,6f,75,74,68,a,6e,6f,72,74,68,a,65,61,73,74,a,6e,6f,72,74,68,a,
  //   73,6f,75,74,68,a,77,65,73,74,a,6e,6f,72,74,68,a,77,65,73,74,a,74,61,6b,65,20,6d,75,
  //   67,a,6e,6f,72,74,68,a,73,6f,75,74,68,a,77,65,73,74,a,65,61,73,74,a,65,61,73,74,a,
  //   65,61,73,74,a,74,61,6b,65,20,63,6f,69,6e,a,6e,6f,72,74,68,a,65,61,73,74,a,77,65,73,
  //   74,a,6e,6f,72,74,68,a,74,61,6b,65,20,68,79,70,65,72,63,75,62,65,a,73,6f,75,74,68,
  //   a,73,6f,75,74,68,a,73,6f,75,74,68,a,65,61,73,74,a,77,65,73,74,a,77,65,73,74,a,74,
  //   61,6b,65,20,61,73,74,72,6f,6c,61,62,65,a,6e,6f,72,74,68,a,65,61,73,74,a,6e,6f,72,
  //   74,68,a,69,6e,76,a,65,61,73,74,a,69,6e,76,a
  //   Instr addr (PC+phase)
  //   PC
  //   nextpc=
  //   pc+phase+1
  //   Instr phase
  //   wait for input
  //   I/O
  //   Instruction decoding
  //   Conditional jumps
  //   Internal registers
  //   ALU
endmodule
