// Digital circuit day5.dig as structural Verilog
module day5 (
  input  clk,
  output [63:0] in_last,
  output [63:0] out_last,
  output [7:0] out_cnt,
  output [7:0] in_cnt
);

  wire intcode_1_p3, intcode_1_p4;
  wire [63:0] input_d, intcode_1_p5;

  Counter #(.Bits(8)) counter_1 (.en(intcode_1_p3), .C(clk), .clr(1'b0), .out(in_cnt));  // open: ovf
  ROM #(.AddrBits(8), .Bits(64)) \input  (.A(in_cnt), .sel(1'b1), .D(input_d));
  // intcode intcode_1: pin names not known; wires that end beside it: clk, input_d, intcode_1_p3, intcode_1_p4, intcode_1_p5, intcode_1_p3
  Register #(.Bits(64)) register_1 (.D(input_d), .C(clk), .en(intcode_1_p3), .Q(in_last));
  Register #(.Bits(64)) register_2 (.D(intcode_1_p5), .C(clk), .en(intcode_1_p4), .Q(out_last));
  Counter #(.Bits(8)) counter_2 (.en(intcode_1_p4), .C(clk), .clr(1'b0), .out(out_cnt));  // open: ovf
  RAMDualPort #(.AddrBits(8), .Bits(64)) \output  (
    .A(out_cnt), .Din(intcode_1_p5), .str(intcode_1_p4), .C(clk), .ld(1'b1));  // open: D

  // Other names for the same wires on the sheet: C = clk

  // Notes on the sheet:
  //   contents of input (hex, n*v repeats v):
  //   5
endmodule
