// Digital circuit day7_amplifier.dig as structural Verilog
module day7_amplifier (
  input  [63:0] phase,
  input  C,
  input  in_en,
  input  [63:0] in_val,
  output [63:0] out_last,
  output out_en,
  output [63:0] out_val,
  output halt
);

  wire fifo_preloaded_1_out_avail, intcode_1_in_req, intcode_1_running, intcode_1_write_en;
  wire [1:0] intcode_1_phase;
  wire [15:0] intcode_1_pc, intcode_1_rw_addr;
  wire [63:0] fifo_preloaded_1_out_val, intcode_1_instr, intcode_1_write_val;

  fifo_preloaded fifo_preloaded_1 (
    .C(C), .\initial (phase), .in_en(in_en), .in_val(in_val), .out_en(intcode_1_in_req),
    .out_avail(fifo_preloaded_1_out_avail), .out_val(fifo_preloaded_1_out_val));  // open: cnt
  intcode #(.generic("ramLabel := \"ram\" + args.label;")) intcode_1 (
    .clock(C), .in_val(fifo_preloaded_1_out_val), .in_avail(fifo_preloaded_1_out_avail),
    .write_val(intcode_1_write_val), .rw_addr(intcode_1_rw_addr), .write_en(intcode_1_write_en),
    .pc(intcode_1_pc), .instr(intcode_1_instr), .phase(intcode_1_phase), .out_en(out_en), .out_val(out_val),
    .running(intcode_1_running), .in_req(intcode_1_in_req));  // open: X, Y, r, cycle_cnt
  // Probe pc on intcode_1_pc
  // Probe instr on intcode_1_instr
  not not_1 (halt, intcode_1_running);
  // Probe write_en on intcode_1_write_en
  Break u_halt (.brk(halt));
  Register #(.Bits(64)) register_1 (.D(out_val), .C(C), .en(out_en), .Q(out_last));
  // Probe w_val on intcode_1_write_val
  // Probe addr on intcode_1_rw_addr
  // Probe phase on intcode_1_phase
  Break out (.brk(out_en));

  // Notes on the sheet:
  //   phase: default 1
endmodule
