// Digital circuit day7part1.dig as structural Verilog
module day7part1 (
  input  clk,
  output [63:0] out3_last,
  output [63:0] out4_last,
  output [63:0] out1_last,
  output [63:0] out2_last,
  output [63:0] out0_last
);

  wire amplifier0_out_en, amplifier1_out_en, amplifier2_out_en, amplifier3_out_en, amplifier4_halt;
  wire [2:0] permuter_1_out_0, permuter_1_out_1, permuter_1_out_2, permuter_1_out_3, permuter_1_out_4;
  wire [63:0] amplifier0_out_val, amplifier1_out_val, amplifier2_out_val, amplifier3_out_val;

  permuter permuter_1 (
    .cnt(7'b0100011), .out_0(permuter_1_out_0), .out_1(permuter_1_out_1), .out_2(permuter_1_out_2),
    .out_3(permuter_1_out_3), .out_4(permuter_1_out_4));
  permuter permuter_2 (
    .cnt(7'b0100011), .out_0(permuter_1_out_0), .out_1(permuter_1_out_1), .out_2(permuter_1_out_2),
    .out_3(permuter_1_out_3), .out_4(permuter_1_out_4));
  day7_amplifier #(.generic("label := \"0\";")) amplifier0 (
    .phase({{61{1'b0}}, permuter_1_out_0}), .C(clk), .in_en(1'b1), .in_val({64{1'b0}}), .out_last(out0_last),
    .out_en(amplifier0_out_en), .out_val(amplifier0_out_val));  // open: halt
  day7_amplifier #(.generic("label := \"1\";")) amplifier1 (
    .phase({{61{1'b0}}, permuter_1_out_1}), .C(clk), .in_en(amplifier0_out_en), .in_val(amplifier0_out_val),
    .out_last(out1_last), .out_en(amplifier1_out_en), .out_val(amplifier1_out_val));  // open: halt
  day7_amplifier #(.generic("label := \"2\";")) amplifier2 (
    .phase({{61{1'b0}}, permuter_1_out_2}), .C(clk), .in_en(amplifier1_out_en), .in_val(amplifier1_out_val),
    .out_last(out2_last), .out_en(amplifier2_out_en), .out_val(amplifier2_out_val));  // open: halt
  day7_amplifier #(.generic("label := \"3\";")) amplifier3 (
    .phase({{61{1'b0}}, permuter_1_out_3}), .C(clk), .in_en(amplifier2_out_en), .in_val(amplifier2_out_val),
    .out_last(out3_last), .out_en(amplifier3_out_en), .out_val(amplifier3_out_val));  // open: halt
  day7_amplifier #(.generic("label := \"4\";")) amplifier4 (
    .phase({{61{1'b0}}, permuter_1_out_4}), .C(clk), .in_en(amplifier3_out_en), .in_val(amplifier3_out_val),
    .out_last(out4_last), .halt(amplifier4_halt));  // open: out_en, out_val
  Break out_4 (.brk(amplifier4_halt));

  // Other names for the same wires on the sheet: C = clk

  // Notes on the sheet:
  //   clk: Hz: 10
endmodule
