// Digital circuit day7part2.dig as structural Verilog
module day7part2 (
  input  clk,
  output [63:0] out3_last,
  output [63:0] out4_last,
  output [63:0] out1_last,
  output [63:0] out2_last,
  output [63:0] out0_last
);

  wire amplifier0_out_en, amplifier1_out_en, amplifier2_out_en, amplifier3_out_en, amplifier4_halt,
       amplifier4_out_en, fifo_preloaded_1_out_avail;
  wire [2:0] permuter_1_out_0, permuter_1_out_1, permuter_1_out_2, permuter_1_out_3, permuter_1_out_4;
  wire [63:0] add_1_s, add_2_s, add_3_s, add_4_s, add_5_s, amplifier0_out_val, amplifier1_out_val,
       amplifier2_out_val, amplifier3_out_val, amplifier4_out_val, fifo_preloaded_1_out_val;

  permuter permuter_1 (
    .cnt(7'b0100100), .out_0(permuter_1_out_0), .out_1(permuter_1_out_1), .out_2(permuter_1_out_2),
    .out_3(permuter_1_out_3), .out_4(permuter_1_out_4));
  fifo_preloaded fifo_preloaded_1 (
    .C(clk), .\initial ({64{1'b0}}), .in_en(amplifier4_out_en), .in_val(amplifier4_out_val),
    .out_en(fifo_preloaded_1_out_avail), .out_avail(fifo_preloaded_1_out_avail),
    .out_val(fifo_preloaded_1_out_val));  // open: cnt
  Add #(.Bits(64)) add_1 (.a({{61{1'b0}}, permuter_1_out_0}), .b(64'h5), .c_i(1'b0), .s(add_1_s));  // open: c_o
  day7_amplifier #(.generic("label := \"0\";")) amplifier0 (
    .phase(add_1_s), .C(clk), .in_en(fifo_preloaded_1_out_avail), .in_val(fifo_preloaded_1_out_val),
    .out_last(out0_last), .out_en(amplifier0_out_en), .out_val(amplifier0_out_val));  // open: halt
  Add #(.Bits(64)) add_2 (.a({{61{1'b0}}, permuter_1_out_1}), .b(64'h5), .c_i(1'b0), .s(add_2_s));  // open: c_o
  day7_amplifier #(.generic("label := \"1\";")) amplifier1 (
    .phase(add_2_s), .C(clk), .in_en(amplifier0_out_en), .in_val(amplifier0_out_val), .out_last(out1_last),
    .out_en(amplifier1_out_en), .out_val(amplifier1_out_val));  // open: halt
  Add #(.Bits(64)) add_3 (.a({{61{1'b0}}, permuter_1_out_2}), .b(64'h5), .c_i(1'b0), .s(add_3_s));  // open: c_o
  day7_amplifier #(.generic("label := \"2\";")) amplifier2 (
    .phase(add_3_s), .C(clk), .in_en(amplifier1_out_en), .in_val(amplifier1_out_val), .out_last(out2_last),
    .out_en(amplifier2_out_en), .out_val(amplifier2_out_val));  // open: halt
  Add #(.Bits(64)) add_4 (.a({{61{1'b0}}, permuter_1_out_3}), .b(64'h5), .c_i(1'b0), .s(add_4_s));  // open: c_o
  day7_amplifier #(.generic("label := \"3\";")) amplifier3 (
    .phase(add_4_s), .C(clk), .in_en(amplifier2_out_en), .in_val(amplifier2_out_val), .out_last(out3_last),
    .out_en(amplifier3_out_en), .out_val(amplifier3_out_val));  // open: halt
  Add #(.Bits(64)) add_5 (.a({{61{1'b0}}, permuter_1_out_4}), .b(64'h5), .c_i(1'b0), .s(add_5_s));  // open: c_o
  day7_amplifier #(.generic("label := \"4\";")) amplifier4 (
    .phase(add_5_s), .C(clk), .in_en(amplifier3_out_en), .in_val(amplifier3_out_val), .out_last(out4_last),
    .out_en(amplifier4_out_en), .out_val(amplifier4_out_val), .halt(amplifier4_halt));
  Break halt_4 (.brk(amplifier4_halt));

  // Other names for the same wires on the sheet: C = clk

  // Notes on the sheet:
  //   clk: Hz: 10
endmodule
