// Digital circuit fifo.dig as structural Verilog
module fifo (
  input  C,
  input  in_en,
  input  [63:0] in_val,
  input  out_en,
  output out_avail,
  output [63:0] out_val,
  output [7:0] cnt
);

  wire comparator_1_eq;
  wire [7:0] in_cnt_out, out_cnt_out;

  Counter #(.Bits(8)) in_cnt (.en(in_en), .C(C), .clr(1'b0), .out(in_cnt_out));  // open: ovf
  Counter #(.Bits(8)) out_cnt (.en(out_en), .C(C), .clr(1'b0), .out(out_cnt_out));  // open: ovf
  RAMDualAccess #(.AddrBits(8), .Bits(64)) ramdualaccess_1 (
    .str(in_en), .C(C), .ld(1'b1), .A1(in_cnt_out), .Din1(in_val), .A2(out_cnt_out), .D2(out_val));  // open: D1
  Comparator #(.Bits(8)) comparator_1 (.a(out_cnt_out), .b(in_cnt_out), .eq(comparator_1_eq));  // open: gt, lt
  Sub #(.Bits(8)) sub_1 (.a(in_cnt_out), .b(out_cnt_out), .c_i(1'b0), .s(cnt));  // open: c_o
  not not_1 (out_avail, comparator_1_eq);
endmodule
