// Digital circuit fifo_preloaded.dig as structural Verilog
module fifo_preloaded (
  input  C,
  input  [63:0] \initial ,
  input  in_en,
  input  [63:0] in_val,
  input  out_en,
  output out_avail,
  output [63:0] out_val,
  output [7:0] cnt
);

  wire and_1_out, fifo_1_out_avail, usefifo_q;
  wire [63:0] fifo_1_out_val;

  fifo fifo_1 (
    .C(C), .in_en(in_en), .in_val(in_val), .out_en(and_1_out), .out_avail(fifo_1_out_avail),
    .out_val(fifo_1_out_val), .cnt(cnt));
  Multiplexer #(.Bits(64)) multiplexer_1 (.sel(usefifo_q), .in_0(\initial ), .in_1(fifo_1_out_val), .out(out_val));
  RS_FF usefifo (.S(out_en), .C(C), .R(1'b0), .Q(usefifo_q));  // open: nQ
  or or_1 (out_avail, ~usefifo_q, fifo_1_out_avail);  // Or
  and and_1 (and_1_out, out_en, usefifo_q, fifo_1_out_avail);

  // Notes on the sheet:
  //   initial: default 3
endmodule
