// Digital circuit intcode.dig as structural Verilog
module intcode (
  input  clock,
  input  [63:0] in_val,
  input  in_avail,
  output [63:0] write_val,
  output [15:0] rw_addr,
  output write_en,
  output [15:0] pc,
  output [63:0] X,
  output [63:0] Y,
  output [63:0] r,
  output [63:0] instr,
  output [1:0] phase,
  output out_en,
  output [63:0] out_val,
  output [31:0] cycle_cnt,
  output running,
  output in_req,
  output [15:0] relbase
);

  wire addbase, advance, and_2_out, and_3_out, and_4_out, and_5_out, and_6_out, and_7_out, and_8_out,
       and_9_out, and_10_out, and_11_out, and_12_out, and_13_out, and_18_out, and_19_out, C, C_t,
       comparator_1_eq, comparator_2_eq, comparator_3_gt, decoder_1_out_0, decoder_1_out_1, decoder_1_out_2,
       decoder_1_out_3, decoder_2_out_1, decoder_2_out_2, decoder_2_out_3, decoder_2_out_4, decoder_2_out_5,
       decoder_2_out_6, decoder_2_out_7, decoder_2_out_8, decoder_2_out_9, indirect, nor_1_out, nor_2_out,
       or_1_out, or_2_out, or_4_out, or_5_out, or_6_out, run_nq, sub_1_c_o, sub_2_c_o, sub_3_c_o, sub_4_c_o,
       sub_5_c_o;
  wire [0:0] lt_2_eq, lt_2_lt;
  wire [3:0] multiplexer_11_out;
  wire [15:0] add_1_s, add_2_s, add_3_s, add_4_s, multiplexer_2_out, multiplexer_3_out, multiplexer_4_out,
       register_1_q;
  wire [63:0] mul_mul, multiplexer_5_out, multiplexer_7_out, multiplexer_8_out, multiplexer_9_out,
       multiplexer_10_out, plus_s, sub_1_s, sub_2_s, sub_3_s, sub_4_s, sub_5_s, write0_last_q;

  Comparator #(.Bits(16)) comparator_1 (.a(rw_addr), .b({16{1'b0}}), .eq(comparator_1_eq));  // open: gt, lt
  RAMDualPort #(.AddrBits(16), .isProgramMemory("true"), .Bits(64), .generic("this.Label=args.ramLabel;")) ram (
    .A(rw_addr), .Din(write_val), .str(write_en), .C(C_t), .ld(1'b1), .D(out_val));
  Break break_1 (.brk(write_en));
  Register #(.Bits(64)) write0_last (.D(write_val), .C(C_t), .en(comparator_1_eq), .Q(write0_last_q));
  // Probe on write0_last_q
  T_FF #(.Default(1)) run (.T(and_5_out), .C(C_t), .Q(running), .nQ(run_nq));
  nand nand_1 (C, running, clock);
  Counter #(.Bits(32)) counter_1 (.en(running), .C(C_t), .clr(1'b0), .out(cycle_cnt));  // open: ovf
  Multiplexer #(.Bits(16)) multiplexer_1 (.sel(C_t), .in_0(register_1_q), .in_1(add_3_s), .out(rw_addr));
  Break halt (.brk(run_nq));
  and and_1 (C_t, running, clock);
  Add #(.Bits(16)) add_1 (.a(multiplexer_2_out), .b(relbase), .c_i(1'b0), .s(add_1_s));  // open: c_o
  Register #(.Bits(16)) register_1 (.D(multiplexer_3_out), .C(C), .en(1'b1), .Q(register_1_q));
  Break write (.brk(write_en));
  Add #(.Bits(16)) add_2 (.a(pc), .b({{14{1'b0}}, phase}), .c_i(1'b1), .s(add_2_s));  // open: c_o
  Add #(.Bits(16)) add_3 (.a({{14{1'b0}}, phase}), .b(pc), .c_i(1'b0), .s(add_3_s));  // open: c_o
  Multiplexer #(.Bits(16)) multiplexer_2 (
    .sel(indirect), .in_0(add_3_s), .in_1(out_val[15:0]), .out(multiplexer_2_out));
  Multiplexer #(.Bits(16)) multiplexer_3 (
    .sel(addbase), .in_0(multiplexer_2_out), .in_1(add_1_s), .out(multiplexer_3_out));
  Multiplexer #(.Bits(16)) multiplexer_4 (
    .sel(or_1_out), .in_0(add_2_s), .in_1(out_val[15:0]), .out(multiplexer_4_out));
  and and_2 (and_2_out, advance, or_2_out);
  Register #(.Bits(16)) register_2 (.D(multiplexer_4_out), .C(C_t), .en(and_2_out), .Q(pc));
  or or_1 (or_1_out, and_4_out, and_3_out);
  or or_2 (or_2_out, out_en, and_7_out, and_18_out, write_en);
  and and_3 (and_3_out, ~comparator_2_eq, decoder_2_out_5);  // And
  and and_4 (and_4_out, comparator_2_eq, decoder_2_out_6);
  Counter #(.Bits(2)) counter_2 (.en(advance), .C(C_t), .clr(and_2_out), .out(phase));  // open: ovf
  Register #(.Bits(64)) register_3 (.D(out_val), .C(C_t), .en(decoder_1_out_0), .Q(instr));
  Decoder #(.Selector_Bits(2)) decoder_1 (
    .sel(phase), .out_0(decoder_1_out_0), .out_1(decoder_1_out_1), .out_2(decoder_1_out_2),
    .out_3(decoder_1_out_3));
  Break jnz (.brk(decoder_2_out_5));
  Break jz (.brk(decoder_2_out_6));
  or or_3 (write_en, in_req, decoder_1_out_3);
  and and_5 (and_5_out, decoder_1_out_1, nor_2_out);
  Sub #(.Bits(64)) sub_1 (.a(instr), .b(64'h4e20), .c_i(1'b0), .s(sub_1_s), .c_o(sub_1_c_o));
  Comparator #(.Signed("true"), .Bits(64)) comparator_2 (.a({64{1'b0}}), .b(X), .eq(comparator_2_eq));  // open: gt, lt
  Multiplexer #(.Bits(64)) multiplexer_5 (.sel(sub_1_c_o), .in_0(sub_1_s), .in_1(instr), .out(multiplexer_5_out));
  and and_6 (and_6_out, ~sub_1_c_o, decoder_1_out_3);  // And
  Multiplexer #(.Bits(64)) multiplexer_6 (.sel(in_req), .in_0(r), .in_1(in_val), .out(write_val));
  Sub #(.Bits(64)) sub_2 (.a(multiplexer_5_out), .b(64'h7d0), .c_i(1'b0), .s(sub_2_s), .c_o(sub_2_c_o));
  Sub #(.Bits(64)) sub_3 (.a(multiplexer_7_out), .b(64'h3e8), .c_i(1'b0), .s(sub_3_s), .c_o(sub_3_c_o));
  and and_7 (and_7_out, or_4_out, decoder_1_out_2);
  Multiplexer #(.Bits(64)) multiplexer_7 (
    .sel(sub_2_c_o), .in_0(sub_2_s), .in_1(multiplexer_5_out), .out(multiplexer_7_out));
  Multiplexer #(.Bits(64)) multiplexer_8 (
    .sel(sub_3_c_o), .in_0(sub_3_s), .in_1(multiplexer_7_out), .out(multiplexer_8_out));
  and and_8 (and_8_out, ~sub_3_c_o, decoder_1_out_2);  // And
  and and_9 (and_9_out, ~sub_2_c_o, decoder_1_out_2);  // And
  and and_10 (and_10_out, in_req, ~in_avail);  // And
  or or_4 (or_4_out, decoder_2_out_5, decoder_2_out_6);
  Sub #(.Bits(64)) sub_4 (.a(multiplexer_8_out), .b(64'hc8), .c_i(1'b0), .s(sub_4_s), .c_o(sub_4_c_o));
  Sub #(.Bits(64)) sub_5 (.a(multiplexer_9_out), .b(64'h64), .c_i(1'b0), .s(sub_5_s), .c_o(sub_5_c_o));
  not not_1 (advance, and_10_out);
  Break in (.brk(in_req));
  Multiplexer #(.Bits(64)) multiplexer_9 (
    .sel(sub_4_c_o), .in_0(sub_4_s), .in_1(multiplexer_8_out), .out(multiplexer_9_out));
  Multiplexer #(.Bits(64)) multiplexer_10 (
    .sel(sub_5_c_o), .in_0(sub_5_s), .in_1(multiplexer_9_out), .out(multiplexer_10_out));
  and and_11 (and_11_out, ~sub_5_c_o, decoder_1_out_1);  // And
  and and_12 (and_12_out, ~sub_4_c_o, decoder_1_out_1);  // And
  or or_5 (or_5_out, and_6_out, and_9_out, and_12_out);
  nor nor_1 (nor_1_out, and_8_out, and_11_out);
  and and_13 (and_13_out, out_en, C);
  Comparator #(.Bits(64)) comparator_3 (.a(multiplexer_10_out), .b(64'h9), .gt(comparator_3_gt));  // open: eq, lt
  or or_6 (or_6_out, nor_1_out, or_5_out);
  and and_14 (in_req, decoder_2_out_3, decoder_1_out_1);
  and and_15 (addbase, or_5_out, ~decoder_1_out_0);  // And
  and and_16 (indirect, or_6_out, ~decoder_1_out_0);  // And
  and and_17 (out_en, decoder_2_out_4, decoder_1_out_1);
  Break out (.brk(and_13_out));
  Multiplexer #(.Bits(4)) multiplexer_11 (
    .sel(comparator_3_gt), .in_0(multiplexer_10_out[3:0]), .in_1(4'b1111), .out(multiplexer_11_out));
  and and_18 (and_18_out, decoder_2_out_9, decoder_1_out_1);
  Decoder #(.Selector_Bits(4)) decoder_2 (
    .sel(multiplexer_11_out), .out_1(decoder_2_out_1), .out_2(decoder_2_out_2), .out_3(decoder_2_out_3),
    .out_4(decoder_2_out_4), .out_5(decoder_2_out_5), .out_6(decoder_2_out_6), .out_7(decoder_2_out_7),
    .out_8(decoder_2_out_8), .out_9(decoder_2_out_9));  // open: out_0, out_10, out_11, out_12, out_13, out_14, out_15
  Break lt (.brk(decoder_2_out_7));
  Register #(.Bits(64)) register_4 (.D(out_val), .C(C_t), .en(decoder_1_out_1), .Q(X));
  Add #(.Bits(64)) plus (.a(X), .b(Y), .c_i(1'b0), .s(plus_s));  // open: c_o
  Comparator #(.Signed("true"), .Bits(64)) lt_2 (.a(X), .b(Y), .eq(lt_2_eq[0]), .lt(lt_2_lt[0]));  // open: gt
  nor nor_2 (nor_2_out, decoder_2_out_1, decoder_2_out_2, decoder_2_out_3, decoder_2_out_4, decoder_2_out_5, decoder_2_out_6, decoder_2_out_7, decoder_2_out_8, decoder_2_out_9);
  Break eq (.brk(decoder_2_out_8));
  Register #(.Bits(64)) register_5 (.D(out_val), .C(C_t), .en(decoder_1_out_2), .Q(Y));
  Mul #(.Signed("true"), .Bits(32)) mul (.a(X[31:0]), .b(Y[31:0]), .mul(mul_mul));
  Multiplexer #(.Selector_Bits(4), .Bits(64)) multiplexer_12 (
    .sel(multiplexer_11_out), .in_0({64{1'b0}}), .in_1(plus_s), .in_2(mul_mul), .in_3({64{1'b0}}),
    .in_4({64{1'b0}}), .in_5({64{1'b0}}), .in_6({64{1'b0}}), .in_7({{63{1'b0}}, lt_2_lt[0]}),
    .in_8({{63{1'b0}}, lt_2_eq[0]}), .in_9({64{1'b0}}), .in_10({64{1'b0}}), .in_11({64{1'b0}}),
    .in_12({64{1'b0}}), .in_13({64{1'b0}}), .in_14({64{1'b0}}), .in_15({64{1'b0}}), .out(r));
  Add #(.Bits(16)) add_4 (.a(relbase), .b(out_val[15:0]), .c_i(1'b0), .s(add_4_s));  // open: c_o
  and and_19 (and_19_out, decoder_2_out_9, decoder_1_out_1);
  Register #(.Bits(16)) register_6 (.D(add_4_s), .C(C_t), .en(and_19_out), .Q(relbase));

  // Other names for the same wires on the sheet: ram_addr_1[15:0] = rw_addr; paramval[63:0] = out_val;
  //   ram_rval_1[63:0] = out_val; ram_we = write_en; ram_wval[63:0] = write_val

  // Notes on the sheet:
  //   clock: Hz: 100
  //   in_val: default 1
  //   in_avail: default 1
  //   param addr
  //   I-fetch (PC+phase)
  //   instr addr
  //   PC
  //   nextpc=
  //   pc+phase+1
  //   Conditional jumps
  //   phase
  //   Instruction complete
  //   Instruction decoding
  //   2-parameter instructions end on phase 2
  //   wait for input
  //   Bad instruction detection
  //   Parameter registers
  //   ALU
endmodule
