// Digital circuit mul64.dig as structural Verilog
module mul64 (
  input  [63:0] a,
  input  [63:0] b,
  output [63:0] mul
);

  wire add_1_c_o, xor_1_out;
  wire [63:0] add_1_s, add_2_s, mul_1_mul, mul_2_mul, mul_3_mul, multiplexer_1_out, multiplexer_2_out,
       neg_1_out, neg_2_out, neg_3_out;

  Neg #(.Bits(64)) neg_1 (.in(a), .out(neg_1_out));
  Neg #(.Bits(64)) neg_2 (.in(b), .out(neg_2_out));
  Multiplexer #(.Bits(64)) multiplexer_1 (.sel(a[63]), .in_0(a), .in_1(neg_1_out), .out(multiplexer_1_out));
  Multiplexer #(.Bits(64)) multiplexer_2 (.sel(b[63]), .in_0(b), .in_1(neg_2_out), .out(multiplexer_2_out));
  xor xor_1 (xor_1_out, a[63], b[63]);
  Mul #(.Bits(32)) mul_1 (.a(multiplexer_1_out[31:0]), .b(multiplexer_2_out[31:0]), .mul(mul_1_mul));
  Mul #(.Bits(32)) mul_2 (.a(multiplexer_1_out[31:0]), .b(multiplexer_2_out[63:32]), .mul(mul_2_mul));
  Mul #(.Bits(32)) mul_3 (.a(multiplexer_1_out[63:32]), .b(multiplexer_2_out[31:0]), .mul(mul_3_mul));
  Add #(.Bits(64)) add_1 (.a(mul_2_mul), .b(mul_3_mul), .c_i(1'b0), .s(add_1_s), .c_o(add_1_c_o));
  Add #(.Bits(64)) add_2 (.a(mul_1_mul), .b({add_1_s[31:0], {32{1'b0}}}), .c_i(add_1_c_o), .s(add_2_s));  // open: c_o
  Neg #(.Bits(64)) neg_3 (.in(add_2_s), .out(neg_3_out));
  Multiplexer #(.Bits(64)) multiplexer_3 (.sel(xor_1_out), .in_0(add_2_s), .in_1(neg_3_out), .out(mul));

  // Notes on the sheet:
  //   a: default 2147483648
  //   b: default 2
endmodule
