// Digital circuit permuter.dig as structural Verilog
module permuter (
  input  [6:0] cnt,
  output [2:0] out_0,
  output [2:0] out_1,
  output [2:0] out_2,
  output [2:0] out_3,
  output [2:0] out_4
);

  wire [2:0] multiplexer_3_out, multiplexer_4_out, multiplexer_6_out, multiplexer_7_out, multiplexer_8_out,
       multiplexer_10_out, multiplexer_12_out, multiplexer_13_out, multiplexer_14_out;
  wire [6:0] div_1_q, div_1_r, div_2_q, div_2_r;

  Div #(.Bits(7)) div_1 (.a(cnt), .b(7'b0011000), .q(div_1_q), .r(div_1_r));
  // Probe on div_1_q
  Multiplexer #(.Selector_Bits(3), .Bits(3)) multiplexer_1 (
    .sel(div_1_q[2:0]), .in_0(3'b000), .in_1(3'b001), .in_2(3'b010), .in_3(3'b011), .in_4(3'b100),
    .in_5(3'b000), .in_6(3'b000), .in_7(3'b000), .out(out_0));
  Multiplexer #(.Bits(3)) multiplexer_2 (
    .sel(div_2_r[0]), .in_0(multiplexer_3_out), .in_1(multiplexer_7_out), .out(out_4));
  Multiplexer #(.Selector_Bits(2), .Bits(3)) multiplexer_3 (
    .sel(div_2_r[2:1]), .in_0(multiplexer_13_out), .in_1(multiplexer_12_out), .in_2(multiplexer_14_out),
    .in_3(3'b000), .out(multiplexer_3_out));
  Multiplexer #(.Selector_Bits(3), .Bits(3)) multiplexer_4 (
    .sel(div_1_q[2:0]), .in_0(3'b100), .in_1(3'b000), .in_2(3'b001), .in_3(3'b010), .in_4(3'b011),
    .in_5(3'b000), .in_6(3'b000), .in_7(3'b000), .out(multiplexer_4_out));
  Multiplexer #(.Bits(3)) multiplexer_5 (
    .sel(div_2_r[0]), .in_0(multiplexer_7_out), .in_1(multiplexer_3_out), .out(out_3));
  Multiplexer #(.Selector_Bits(3), .Bits(3)) multiplexer_6 (
    .sel(div_1_q[2:0]), .in_0(3'b011), .in_1(3'b100), .in_2(3'b000), .in_3(3'b001), .in_4(3'b010),
    .in_5(3'b000), .in_6(3'b000), .in_7(3'b000), .out(multiplexer_6_out));
  Multiplexer #(.Selector_Bits(2), .Bits(3)) multiplexer_7 (
    .sel(div_2_r[2:1]), .in_0(multiplexer_12_out), .in_1(multiplexer_14_out), .in_2(multiplexer_13_out),
    .in_3(3'b000), .out(multiplexer_7_out));
  Multiplexer #(.Selector_Bits(3), .Bits(3)) multiplexer_8 (
    .sel(div_1_q[2:0]), .in_0(3'b010), .in_1(3'b011), .in_2(3'b100), .in_3(3'b000), .in_4(3'b001),
    .in_5(3'b000), .in_6(3'b000), .in_7(3'b000), .out(multiplexer_8_out));
  Multiplexer #(.Selector_Bits(2), .Bits(3)) multiplexer_9 (
    .sel(div_2_r[2:1]), .in_0(multiplexer_14_out), .in_1(multiplexer_13_out), .in_2(multiplexer_12_out),
    .in_3(3'b000), .out(out_2));
  Multiplexer #(.Selector_Bits(3), .Bits(3)) multiplexer_10 (
    .sel(div_1_q[2:0]), .in_0(3'b001), .in_1(3'b010), .in_2(3'b011), .in_3(3'b100), .in_4(3'b000),
    .in_5(3'b000), .in_6(3'b000), .in_7(3'b000), .out(multiplexer_10_out));
  // Probe on div_2_r
  Multiplexer #(.Selector_Bits(2), .Bits(3)) multiplexer_11 (
    .sel(div_2_q[1:0]), .in_0(multiplexer_10_out), .in_1(multiplexer_8_out), .in_2(multiplexer_6_out),
    .in_3(multiplexer_4_out), .out(out_1));
  Multiplexer #(.Selector_Bits(2), .Bits(3)) multiplexer_12 (
    .sel(div_2_q[1:0]), .in_0(multiplexer_4_out), .in_1(multiplexer_10_out), .in_2(multiplexer_8_out),
    .in_3(multiplexer_6_out), .out(multiplexer_12_out));
  Multiplexer #(.Selector_Bits(2), .Bits(3)) multiplexer_13 (
    .sel(div_2_q[1:0]), .in_0(multiplexer_6_out), .in_1(multiplexer_4_out), .in_2(multiplexer_10_out),
    .in_3(multiplexer_8_out), .out(multiplexer_13_out));
  Multiplexer #(.Selector_Bits(2), .Bits(3)) multiplexer_14 (
    .sel(div_2_q[1:0]), .in_0(multiplexer_8_out), .in_1(multiplexer_6_out), .in_2(multiplexer_4_out),
    .in_3(multiplexer_10_out), .out(multiplexer_14_out));
  // Probe on div_1_r
  Div #(.Bits(7)) div_2 (.a(div_1_r), .b(7'b0000110), .q(div_2_q), .r(div_2_r));
  // Probe on div_2_q
endmodule

/* Test case permutations_test:
cnt  out_0  out_1  out_2  out_3  out_4
1    0      1      2      3      4
2    0      1      3      2      4
3    0      1      3      4      2
4    0      1      4      3      2
5    0      1      4      2      3
6    0      2      3      1      4
7    0      2      3      4      1
8    0      2      4      3      1
9    0      2      4      1      3
10   0      2      1      4      3
11   0      2      1      3      4
12   0      3      4      2      1
13   0      3      4      1      2
14   0      3      1      4      2
15   0      3      1      2      4
16   0      3      2      1      4
17   0      3      2      4      1
18   0      4      1      3      2
19   0      4      1      2      3
20   0      4      2      1      3
21   0      4      2      3      1
22   0      4      3      2      1
23   0      4      3      1      2
24   1      2      3      0      4
25   1      2      3      4      0
26   1      2      4      3      0
27   1      2      4      0      3
28   1      2      0      4      3
29   1      2      0      3      4
30   1      3      4      2      0
31   1      3      4      0      2
32   1      3      0      4      2
33   1      3      0      2      4
34   1      3      2      0      4
35   1      3      2      4      0
36   1      4      0      3      2
37   1      4      0      2      3
38   1      4      2      0      3
39   1      4      2      3      0
40   1      4      3      2      0
41   1      4      3      0      2
42   1      0      2      4      3
43   1      0      2      3      4
44   1      0      3      2      4
45   1      0      3      4      2
46   1      0      4      3      2
47   1      0      4      2      3
48   2      3      4      1      0
49   2      3      4      0      1
50   2      3      0      4      1
51   2      3      0      1      4
52   2      3      1      0      4
53   2      3      1      4      0
54   2      4      0      3      1
55   2      4      0      1      3
56   2      4      1      0      3
57   2      4      1      3      0
58   2      4      3      1      0
59   2      4      3      0      1
60   2      0      1      4      3
61   2      0      1      3      4
62   2      0      3      1      4
63   2      0      3      4      1
64   2      0      4      3      1
65   2      0      4      1      3
66   2      1      3      0      4
67   2      1      3      4      0
68   2      1      4      3      0
69   2      1      4      0      3
70   2      1      0      4      3
71   2      1      0      3      4
72   3      4      0      2      1
73   3      4      0      1      2
74   3      4      1      0      2
75   3      4      1      2      0
76   3      4      2      1      0
77   3      4      2      0      1
78   3      0      1      4      2
79   3      0      1      2      4
80   3      0      2      1      4
81   3      0      2      4      1
82   3      0      4      2      1
83   3      0      4      1      2
84   3      1      2      0      4
85   3      1      2      4      0
86   3      1      4      2      0
87   3      1      4      0      2
88   3      1      0      4      2
89   3      1      0      2      4
90   3      2      4      1      0
91   3      2      4      0      1
92   3      2      0      4      1
93   3      2      0      1      4
94   3      2      1      0      4
95   3      2      1      4      0
96   4      0      1      3      2
97   4      0      1      2      3
98   4      0      2      1      3
99   4      0      2      3      1
100  4      0      3      2      1
101  4      0      3      1      2
102  4      1      2      0      3
103  4      1      2      3      0
104  4      1      3      2      0
105  4      1      3      0      2
106  4      1      0      3      2
107  4      1      0      2      3
108  4      2      3      1      0
109  4      2      3      0      1
110  4      2      0      3      1
111  4      2      0      1      3
112  4      2      1      0      3
113  4      2      1      3      0
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*/
