// Digital circuit shifter.dig as structural Verilog
module shifter (
  input  in_en,
  input  [63:0] in_val,
  input  C,
  output [63:0] out_0,
  output [63:0] out_1,
  output [63:0] out_2,
  output [63:0] out_3,
  output [63:0] out_4,
  output [63:0] out_5,
  output [63:0] out_6,
  output [63:0] out_7
);

  Register #(.Bits(64)) register_1 (.D(in_val), .C(C), .en(in_en), .Q(out_0));
  Register #(.Bits(64)) register_2 (.D(out_0), .C(C), .en(in_en), .Q(out_1));
  Register #(.Bits(64)) register_3 (.D(out_1), .C(C), .en(in_en), .Q(out_2));
  Register #(.Bits(64)) register_4 (.D(out_2), .C(C), .en(in_en), .Q(out_3));
  Register #(.Bits(64)) register_5 (.D(out_3), .C(C), .en(in_en), .Q(out_4));
  Register #(.Bits(64)) register_6 (.D(out_4), .C(C), .en(in_en), .Q(out_5));
  Register #(.Bits(64)) register_7 (.D(out_5), .C(C), .en(in_en), .Q(out_6));
  Register #(.Bits(64)) register_8 (.D(out_6), .C(C), .en(in_en), .Q(out_7));
  // Pins of 1 and 64 bits meet at out_0
  // Pins of 1 and 64 bits meet at out_1
  // Pins of 1 and 64 bits meet at out_2
  // Pins of 1 and 64 bits meet at out_3
  // Pins of 1 and 64 bits meet at out_4
  // Pins of 1 and 64 bits meet at out_5
  // Pins of 1 and 64 bits meet at out_6
  // Pins of 1 and 64 bits meet at out_7

  // Notes on the sheet:
  //   in_val: default 6
endmodule
